// Logisim project Final Project.circ as structural Verilog: 66 circuits, main circuit main
module main (
  output [4:0] Flags
);

  wire CLOCK_out, demultiplexer_1_out0, demultiplexer_1_out1, enable_keyboards_1_en_1,
       enable_keyboards_1_en_2, getchar_operation_1_getchar_op, K1, K2, not_1_out,
       op_control_1__1___current_line_is_halt, op_control_1_call_return_operation,
       op_control_1_enable_disable_flags, op_control_1_enable_disable_register_file,
       op_control_1_flag_manipulation, op_control_1_load_operation, op_control_1_op_select,
       op_control_1_store_operation, putchar_operation_1_putchar_op,
       which_terminal_1__1___print_to_terminal_1__0___term_2,
       which_terminal_1__1___print_to_terminal_1__0___term_2_2;
  wire [3:0] op_control_1_destination_address__always_bits_8_11___if_getchar__make_it_bits_0_3,
       op_control_1_operand_1_address__bits_4_7_if_arithmetic_bitwise_call_return__destination_address_otherwise,
       op_control_1_operand_2_address__always_bits_0_3;
  wire [4:0] alsu_1_final_updated_flags, load_flags_1_updated_flags,
       setting_restoring_flags_1_updated_flags__set_restore;
  wire [6:0] keyboard_1_data, keyboard_2_data;
  wire [15:0] alsu_1_final_result__could_be_getchar_data, bit_extender_1_out, bit_extender_2_out,
       branching_control_1_new_value_of_pc, interrupt_opcode_1_new_opcode, multiplexer_1_out, ram_1_data,
       rb_o_1_rb___o, register_file_1_r1, register_file_1_r2, register_file_1_r3, register_file_1_r4,
       register_file_1_r5, register_file_1_r6, register_file_1_r7, register_file_1_r8, register_file_1_r9,
       register_file_1_r10, register_file_1_r11, register_file_1_r12, register_file_1_r13,
       register_file_1_r14, register_file_1_r15, register_file_1_rd1, register_file_1_rd2,
       register_file_1_rd3, rom_1_data, shadow_pc_1_output_value;

  Clock CLOCK (.out(CLOCK_out));
  not not_1 (not_1_out, op_control_1__1___current_line_is_halt);
  Flags flags_1 (
    .Current_Flags__from_ALSU(alsu_1_final_updated_flags),
    .Current_Flags__from_Manipulation(setting_restoring_flags_1_updated_flags__set_restore),
    .Flag_Manipulation(op_control_1_flag_manipulation), .LOAD_Operation(op_control_1_load_operation),
    .Current_Flags__from_LOAD(load_flags_1_updated_flags), .OpCode(interrupt_opcode_1_new_opcode),
    .Updated_Flags(Flags));
  Keyboard keyboard_1 (.clk(CLOCK_out), .re(enable_keyboards_1_en_1), .avail(K1), .data(keyboard_1_data));  // open: clr
  Keyboard keyboard_2 (.clk(CLOCK_out), .re(enable_keyboards_1_en_2), .avail(K2), .data(keyboard_2_data));  // open: clr
  Enable_Keyboards enable_keyboards_1 (
    .Getchar_op(getchar_operation_1_getchar_op),
    .Which_terminal(which_terminal_1__1___print_to_terminal_1__0___term_2), .EN_1(enable_keyboards_1_en_1),
    .EN_2(enable_keyboards_1_en_2));
  Getchar_Operation getchar_operation_1 (
    .Op_Code(interrupt_opcode_1_new_opcode), .Getchar_op(getchar_operation_1_getchar_op));
  Shadow_PC shadow_pc_1 (
    .Set_Value(branching_control_1_new_value_of_pc), .CLOCK(CLOCK_out),
    .OpCode(interrupt_opcode_1_new_opcode), .EN(not_1_out), .Output_Value(shadow_pc_1_output_value));
  Load_Flags load_flags_1 (.Current_Flags(Flags), .M_Rb___o(ram_1_data), .Updated_Flags(load_flags_1_updated_flags));
  Which_Terminal which_terminal_1 (
    .Op_Code(register_file_1_rd1),
    ._1___Print_to_terminal_1__0___Term_2(which_terminal_1__1___print_to_terminal_1__0___term_2),
    ._1___Print_to_terminal_1__0___Term_2_2(which_terminal_1__1___print_to_terminal_1__0___term_2_2));
  Putchar_Operation putchar_operation_1 (
    .Op_Code(interrupt_opcode_1_new_opcode), .Putchar_op(putchar_operation_1_putchar_op));
  Branching_Control branching_control_1 (
    .Op_Code(interrupt_opcode_1_new_opcode), .Contents_of_Rb(register_file_1_rd2),
    .Current_Value_of_PC(shadow_pc_1_output_value), .Current_Flags(Flags),
    .New_Value_of_PC(branching_control_1_new_value_of_pc), .CALL_RETURN(op_control_1_call_return_operation));
  Setting_Restoring_Flags setting_restoring_flags_1 (
    .Op_Code(interrupt_opcode_1_new_opcode), .Current_Flags(Flags),
    .Updated_Flags__Set_Restore(setting_restoring_flags_1_updated_flags__set_restore),
    .Contents_of_Rd(register_file_1_rd1));
  ALSU alsu_1 (
    .Operand_1(register_file_1_rd1), .Operand_2(register_file_1_rd2), .Current_Flags(Flags),
    .Op_Code(interrupt_opcode_1_new_opcode), .Final_Updated_Flags(alsu_1_final_updated_flags),
    .Op_Select(op_control_1_op_select),
    .Final_Result__could_be_Getchar_data(alsu_1_final_result__could_be_getchar_data),
    .GetChar_Data(multiplexer_1_out));
  ROM #(.addrWidth(16), .dataWidth(16)) rom_1 (.addr(shadow_pc_1_output_value), .data(rom_1_data));  // open: sel
  assign bit_extender_1_out = {{9{1'b0}}, keyboard_1_data};  // Bit_Extender bit_extender_1
  assign bit_extender_2_out = {{9{1'b0}}, keyboard_2_data};  // Bit_Extender bit_extender_2
  Interrupt_Opcode interrupt_opcode_1 (
    .OpCode(rom_1_data), .K2_Interrupt(K2), .K1_Interrupt(K1), .CLOCK(CLOCK_out),
    .New_Opcode(interrupt_opcode_1_new_opcode));
  Multiplexer #(.width(16)) multiplexer_1 (
    .in0(bit_extender_2_out), .in1(bit_extender_1_out), .out(multiplexer_1_out),
    .sel(which_terminal_1__1___print_to_terminal_1__0___term_2_2));  // open: en
  Demultiplexer demultiplexer_1 (
    .out0(demultiplexer_1_out0), .out1(demultiplexer_1_out1), .in(putchar_operation_1_putchar_op),
    .sel(which_terminal_1__1___print_to_terminal_1__0___term_2_2));  // open: en
  // Probe on interrupt_opcode_1_new_opcode
  Rb___o rb_o_1 (.Op_Code(interrupt_opcode_1_new_opcode), .Contents_of_Rb(register_file_1_rd2), .Rb___o(rb_o_1_rb___o));
  Op_Control op_control_1 (
    .Op_Code(interrupt_opcode_1_new_opcode),
    .Operand_1_Address__bits_4_7_if_arithmetic_bitwise_call_return__Destination_Address_otherwise(op_control_1_operand_1_address__bits_4_7_if_arithmetic_bitwise_call_return__destination_address_otherwise),
    .Operand_2_Address__always_bits_0_3(op_control_1_operand_2_address__always_bits_0_3),
    .Destination_Address__always_bits_8_11___if_Getchar__make_it_bits_0_3(op_control_1_destination_address__always_bits_8_11___if_getchar__make_it_bits_0_3),
    .Op_Select(op_control_1_op_select),
    .Enable_Disable_Register_File(op_control_1_enable_disable_register_file),
    .Enable_Disable_Flags(op_control_1_enable_disable_flags),
    ._1___Current_line_is_HALT(op_control_1__1___current_line_is_halt),
    .Flag_Manipulation(op_control_1_flag_manipulation), .STORE_Operation(op_control_1_store_operation),
    .LOAD_Operation(op_control_1_load_operation), .CALL_RETURN_Operation(op_control_1_call_return_operation));  // open: Putchar_Operation, Getchar_Operation
  Register_File register_file_1 (
    .WD1__ALSU(alsu_1_final_result__could_be_getchar_data), .EN1(op_control_1_enable_disable_register_file),
    .WA1(op_control_1_destination_address__always_bits_8_11___if_getchar__make_it_bits_0_3), .S(1'b1),
    .RA1(op_control_1_operand_1_address__bits_4_7_if_arithmetic_bitwise_call_return__destination_address_otherwise),
    .RA2(op_control_1_operand_2_address__always_bits_0_3), .RD1(register_file_1_rd1),
    .RD2(register_file_1_rd2), .LOAD_Op(op_control_1_load_operation), .RA3(4'b1110),
    .RD3(register_file_1_rd3), .EN2_3(op_control_1_call_return_operation), .WA2__FP(4'b1110),
    .WA3__Ra(op_control_1_operand_1_address__bits_4_7_if_arithmetic_bitwise_call_return__destination_address_otherwise),
    .WD1__LOAD(ram_1_data), .WD2__Ra(register_file_1_rd1), .WD3__FP(register_file_1_rd3),
    .WD1__PC___1(shadow_pc_1_output_value), .CALL_RETURN(op_control_1_call_return_operation),
    .WA1__Rb(op_control_1_operand_2_address__always_bits_0_3), .R1(register_file_1_r1),
    .R2(register_file_1_r2), .R3(register_file_1_r3), .R4(register_file_1_r4), .R5(register_file_1_r5),
    .R6(register_file_1_r6), .R7(register_file_1_r7), .R8(register_file_1_r8), .R9(register_file_1_r9),
    .R10(register_file_1_r10), .R11(register_file_1_r11), .R12(register_file_1_r12),
    .R13(register_file_1_r13), .R14(register_file_1_r14), .R15(register_file_1_r15),
    .OpCode(interrupt_opcode_1_new_opcode));
  TTY tty_1 (.data(register_file_1_rd2[6:0]), .clk(CLOCK_out), .we(demultiplexer_1_out1));  // open: clr
  TTY tty_2 (.data(register_file_1_rd2[6:0]), .clk(CLOCK_out), .we(demultiplexer_1_out0));  // open: clr
  RAM #(.addrWidth(16), .dataWidth(16), .bus("separate")) ram_1 (
    .addr(rb_o_1_rb___o), .din(register_file_1_rd1), .data(ram_1_data), .str(op_control_1_store_operation),
    .clk(CLOCK_out));  // open: sel, ld, clr
  // Probe on register_file_1_r1
  // Probe on register_file_1_r2
  // Probe on register_file_1_r3
  // Probe on register_file_1_r4
  // Probe on register_file_1_r5
  // Probe on register_file_1_r6
  // Probe on register_file_1_r7
  // Probe on register_file_1_r8
  // Probe on register_file_1_r9
  // Probe on register_file_1_r10
  // Probe on register_file_1_r11
  // Probe on register_file_1_r12
  // Probe on register_file_1_r13
  // Probe on register_file_1_r14
  // Probe on register_file_1_r15

  // Notes on the sheet:
  //   LOAD / HALT
  //   Flags
  //   Program Counter
  //   HALT?
  //   Branching
  //   Control
  //   Flag
  //   Manipulation
  //   LOAD Flags
  //   Keyboard 1
  //   Keyboard 2
  //   Which terminal/board?
  //   ALSU
  //   CS356: Concurrency & Co-Design
  //   Team Blue
  //   Stored Program (ROM)
  //   contents of rom_1 (hex, n*v repeats v):
  //   eb3b fb00 100b e510 f500 3068 b025 eb13 fb00 190b e101 f100 ed3e fd00 20cd ed41 fd00 20cd 2300 e100
  //   f100 ed3e fd00 20cd 3068 b020 eb37 fb00 180b e40a f400 3068 b024 eb2c fb00 180b e400 f4d0 4304 3380
  //   a543 6205 6304 2300 e100 f100 e200 f2d0 ed44 fd00 20cd e200 f2d0 6002 2300 2300 e346 f300 2803 eb3b
  //   fb00 100b 2c12 21cd 0 2812 21cd 0 99c0 9ad0 9320 4403 eb55 fb00 180b 3380 4203 3380 ed41 fd00 20cd
  //   34c0 eb4c fb00 190b 219a
  //   WD 123
  //   Operation
  //   Control
  //   RA 123
  //   RD 123
  //   Rb+ o
  //   WA 123
  //   Register File
  //   (RAM)
  //   HERA Memory
  //   Carry block; carry; overflow; zero; sign
  //   R1
  //   R2
  //   R3
  //   R4
  //   R5
  //   R6
  //   R7
  //   Terminal 1
  //   Terminal 2
  //   R8
  //   R9
  //   R10
  //   R11
  //   R12
  //   R13
  //   R14
  //   R15
  //   R2 holds interrupt type
  //   Interrupt program stored in 0180
endmodule

module Register_File (
  input  [15:0] WD1__ALSU,
  input  [15:0] WD1__LOAD,
  input  LOAD_Op,
  input  [15:0] WD1__PC___1,
  input  [3:0] WA1,
  input  [15:0] OpCode,
  input  [3:0] WA1__Rb,
  input  EN1,
  input  [15:0] WD2__Ra,
  input  [3:0] WA2__FP,
  input  [15:0] WD3__FP,
  input  [3:0] WA3__Ra,
  input  EN2_3,
  input  CALL_RETURN,
  input  S,
  input  [3:0] RA1,
  input  [3:0] RA2,
  input  [3:0] RA3,
  output [15:0] R1,
  output [15:0] R2,
  output [15:0] R3,
  output [15:0] R4,
  output [15:0] R5,
  output [15:0] R6,
  output [15:0] R7,
  output [15:0] RD1,
  output [15:0] RD2,
  output [15:0] RD3,
  output [15:0] R8,
  output [15:0] R9,
  output [15:0] R10,
  output [15:0] R11,
  output [15:0] R12,
  output [15:0] R13,
  output [15:0] R14,
  output [15:0] R15
);

  wire _1, _1a, _1b, _2, _2a, _2b, _3, _3a, _3b, _4, _4a, _4b, _5, _5a, _5b, _6, _6a, _6b, _7, _7a, _7b, _8,
       _8a, _8b, _9, _9a, _9b, _10, _10a, _10b, _11, _11a, _11b, _12, _12a, _12b, _13, _13a, _13b, _14, _14a,
       _14b, _15, _15a, _15b, a, b, c, CLOCK_out, d, e, f, g, h, i, j, k, l, m, n, o, or_1_out,
       start_interrupt_1_start_interrupt;
  wire [3:0] multiplexer_7_out, multiplexer_8_out, multiplexer_9_out, multiplexer_10_out;
  wire [15:0] aa, ab, ac, ad, adder_1_out, bit_extender_1_out, multiplexer_1_out, multiplexer_3_out, p, q, r,
       register_1_q, s_t, t, u, v, w, WD1, x, y, z;

  Clock CLOCK (.out(CLOCK_out));
  Multiplexer #(.width(16)) multiplexer_1 (
    .in0(WD1__ALSU), .in1(WD1__LOAD), .out(multiplexer_1_out), .sel(LOAD_Op));  // open: en
  Multiplexer #(.width(16)) multiplexer_2 (
    .in0(multiplexer_1_out), .in1(adder_1_out), .out(WD1), .sel(CALL_RETURN));  // open: en
  Adder #(.width(16)) adder_1 (.a(WD1__PC___1), .b(16'h1), .out(adder_1_out));  // open: cin, cout
  assign bit_extender_1_out = {{8{1'b0}}, OpCode[7:0]};  // Bit_Extender bit_extender_1
  Multiplexer #(.width(16)) multiplexer_3 (
    .in0(q), .in1(bit_extender_1_out), .out(multiplexer_3_out), .sel(start_interrupt_1_start_interrupt));  // open: en
  or or_1 (or_1_out, b, start_interrupt_1_start_interrupt);
  Start_Interrupt start_interrupt_1 (.Op_Code(OpCode), .Start_Interrupt(start_interrupt_1_start_interrupt));
  Register #(.width(16)) register_1 (.D({16{1'b0}}), .en(1'b0), .Q(register_1_q), .clk(CLOCK_out));  // open: clr
  Shadow_Registers shadow_registers_1 (.Set_Value(p), .CLOCK(CLOCK_out), .OpCode(OpCode), .EN(a), .Output_Value(R1));
  Shadow_Registers shadow_registers_2 (
    .Set_Value(multiplexer_3_out), .CLOCK(CLOCK_out), .OpCode(OpCode), .EN(or_1_out), .Output_Value(R2));
  Shadow_Registers shadow_registers_3 (.Set_Value(r), .CLOCK(CLOCK_out), .OpCode(OpCode), .EN(c), .Output_Value(R3));
  Shadow_Registers shadow_registers_4 (.Set_Value(s_t), .CLOCK(CLOCK_out), .OpCode(OpCode), .EN(d), .Output_Value(R4));
  Shadow_Registers shadow_registers_5 (.Set_Value(t), .CLOCK(CLOCK_out), .OpCode(OpCode), .EN(e), .Output_Value(R5));
  Shadow_Registers shadow_registers_6 (.Set_Value(u), .CLOCK(CLOCK_out), .OpCode(OpCode), .EN(f), .Output_Value(R6));
  Shadow_Registers shadow_registers_7 (.Set_Value(v), .CLOCK(CLOCK_out), .OpCode(OpCode), .EN(g), .Output_Value(R7));
  Shadow_Registers shadow_registers_8 (.Set_Value(w), .CLOCK(CLOCK_out), .OpCode(OpCode), .EN(h), .Output_Value(R8));
  Shadow_Registers shadow_registers_9 (.Set_Value(x), .CLOCK(CLOCK_out), .OpCode(OpCode), .EN(i), .Output_Value(R9));
  Shadow_Registers shadow_registers_10 (.Set_Value(y), .CLOCK(CLOCK_out), .OpCode(OpCode), .EN(j), .Output_Value(R10));
  Shadow_Registers shadow_registers_11 (.Set_Value(z), .CLOCK(CLOCK_out), .OpCode(OpCode), .EN(k), .Output_Value(R11));
  Shadow_Registers shadow_registers_12 (.Set_Value(aa), .CLOCK(CLOCK_out), .OpCode(OpCode), .EN(l), .Output_Value(R12));
  Shadow_Registers shadow_registers_13 (.Set_Value(ab), .CLOCK(CLOCK_out), .OpCode(OpCode), .EN(m), .Output_Value(R13));
  Shadow_Registers shadow_registers_14 (.Set_Value(ac), .CLOCK(CLOCK_out), .OpCode(OpCode), .EN(n), .Output_Value(R14));
  Shadow_Registers shadow_registers_15 (.Set_Value(ad), .CLOCK(CLOCK_out), .OpCode(OpCode), .EN(o), .Output_Value(R15));
  Multiplexer #(.select(4), .width(16)) multiplexer_4 (
    .in0(register_1_q), .in1(R1), .in2(R2), .in3(R3), .in4(R4), .in5(R5), .in6(R6), .in7(R7), .in8(R8),
    .in9(R9), .in10(R10), .in11(R11), .in12(R12), .in13(R13), .in14(R14), .in15(R15), .out(RD1), .sel(RA1));  // open: en
  Multiplexer #(.select(4), .width(16)) multiplexer_5 (
    .in0(register_1_q), .in1(R1), .in2(R2), .in3(R3), .in4(R4), .in5(R5), .in6(R6), .in7(R7), .in8(R8),
    .in9(R9), .in10(R10), .in11(R11), .in12(R12), .in13(R13), .in14(R14), .in15(R15), .out(RD2), .sel(RA2));  // open: en
  Multiplexer #(.select(4), .width(16)) multiplexer_6 (
    .in0(register_1_q), .in1(R1), .in2(R2), .in3(R3), .in4(R4), .in5(R5), .in6(R6), .in7(R7), .in8(R8),
    .in9(R9), .in10(R10), .in11(R11), .in12(R12), .in13(R13), .in14(R14), .in15(R15), .out(RD3), .sel(RA3));  // open: en
  Decoder #(.select(4)) decoder_1 (
    .out1(_1), .out2(_2), .out3(_3), .out4(_4), .out5(_5), .out6(_6), .out7(_7), .out8(_8), .out9(_9),
    .out10(_10), .out11(_11), .out12(_12), .out13(_13), .out14(_14), .out15(_15), .sel(multiplexer_7_out),
    .en(EN1));  // open: out0
  Multiplexer #(.width(4)) multiplexer_7 (.in1(multiplexer_8_out), .out(multiplexer_7_out), .sel(S));  // open: in0, en
  Multiplexer #(.width(4)) multiplexer_8 (
    .in0(WA1), .in1(WA1__Rb), .out(multiplexer_8_out), .sel(CALL_RETURN));  // open: en
  Decoder #(.select(4)) decoder_2 (
    .out1(_1a), .out2(_2a), .out3(_3a), .out4(_4a), .out5(_5a), .out6(_6a), .out7(_7a), .out8(_8a),
    .out9(_9a), .out10(_10a), .out11(_11a), .out12(_12a), .out13(_13a), .out14(_14a), .out15(_15a),
    .sel(multiplexer_9_out), .en(EN2_3));  // open: out0
  Multiplexer #(.width(4)) multiplexer_9 (.in1(WA2__FP), .out(multiplexer_9_out), .sel(S));  // open: in0, en
  Decoder #(.select(4)) decoder_3 (
    .out1(_1b), .out2(_2b), .out3(_3b), .out4(_4b), .out5(_5b), .out6(_6b), .out7(_7b), .out8(_8b),
    .out9(_9b), .out10(_10b), .out11(_11b), .out12(_12b), .out13(_13b), .out14(_14b), .out15(_15b),
    .sel(multiplexer_10_out), .en(EN2_3));  // open: out0
  Multiplexer #(.width(4)) multiplexer_10 (.in1(WA3__Ra), .out(multiplexer_10_out), .sel(S));  // open: in0, en
  Register_SubCircuit register_subcircuit_1 (
    .EN1(EN1), .EN2_3(EN2_3), .Input_1(_1), .Input_2(_2), .Input_3(_3), .Input_4(_4), .Input_5(_5),
    .Input_6(_6), .Input_7(_7), .Input_8(_8), .Input_9(_9), .Input_10(_10), .Input_11(_11), .Input_12(_12),
    .Input_13(_13), .Input_14(_14), .Input_15(_15), .Input_1_2(_1a), .Input_2_2(_2a), .Input_3_2(_3a),
    .Input_4_2(_4a), .Input_5_2(_5a), .Input_6_2(_6a), .Input_7_2(_7a), .Input_8_2(_8a), .Input_9_2(_9a),
    .Input_10_2(_10a), .Input_11_2(_11a), .Input_12_2(_12a), .Input_13_2(_13a), .Input_14_2(_14a),
    .Input_15_2(_15a), .Input_1_3(_1b), .Input_2_3(_2b), .Input_3_3(_3b), .Input_4_3(_4b), .Input_5_3(_5b),
    .Input_6_3(_6b), .Input_7_3(_7b), .Input_8_3(_8b), .Input_9_3(_9b), .Input_10_3(_10b), .Input_11_3(_11b),
    .Input_12_3(_12b), .Input_13_3(_13b), .Input_14_3(_14b), .Input_15_3(_15b), .WD1(WD1), .WD2(WD2__Ra),
    .WD3(WD3__FP), .R1_EN(a), .R2_EN(b), .R3_EN(c), .R4_EN(d), .R5__EN(e), .R6_EN(f), .R7_EN(g), .R8_EN(h),
    .R9_EN(i), .R10_EN(j), .R11_EN(k), .R12_EN(l), .R13_EN(m), .R14_EN(n), .R15_EN(o), .R1_WD(p), .R2_WD(q),
    .R3_WD(r), .R4_WD(s_t), .R5_WD(t), .R6_WD(u), .R7_WD(v), .R8_WD(w), .R9_WD(x), .R10_WD(y), .R11_WD(z),
    .R12_WD(aa), .R13_WD(ab), .R14_WD(ac), .R15_WD(ad));

  // Other names for the same wires on the sheet: C_R = CALL_RETURN; EN2 = EN2_3; WD2[15:0] = WD2__Ra;
  //   WD3[15:0] = WD3__FP

  // Notes on the sheet:
  //   ASYNCHRONOUS RAM (Register File)
  //   16 16-bit registers
endmodule

module Interrupt_Opcode (
  input  [15:0] OpCode,
  input  K2_Interrupt,
  input  K1_Interrupt,
  input  CLOCK,
  output [15:0] New_Opcode
);

  wire and_1_out, and_2_out, and_3_out, and_4_out, multiplexer_2_out, not_1_out, not_2_out, not_3_out,
       or_1_out, or_2_out, return_from_interrupt_1_return_from_interrupt, s_r_ff_1_q, SWI_start_interrupt,
       t_ff_1_q;
  wire [15:0] multiplexer_1_out, multiplexer_3_out;

  and and_1 (and_1_out, K2_Interrupt, K1_Interrupt, CLOCK);
  // Probe on OpCode
  T_Flip_Flop t_ff_1 (.clk(and_1_out), .T(1'b1), .Q(t_ff_1_q), .en(1'b1));  // open: Qn, preset, reset
  and and_2 (and_2_out, K2_Interrupt, K1_Interrupt);
  not not_1 (not_1_out, and_2_out);
  Start_Interrupt SWI (.Op_Code(OpCode), .Start_Interrupt(SWI_start_interrupt));
  Return_from_Interrupt return_from_interrupt_1 (
    .Op_Code(OpCode), .Return_From_Interrupt(return_from_interrupt_1_return_from_interrupt));
  Multiplexer #(.width(16)) multiplexer_1 (
    .in0(16'h2210), .in1(16'h2211), .out(multiplexer_1_out), .sel(multiplexer_2_out));  // open: en
  Multiplexer #(.enable("false")) multiplexer_2 (
    .in0(t_ff_1_q), .in1(K2_Interrupt), .out(multiplexer_2_out), .sel(not_1_out));
  or or_1 (or_1_out, or_2_out, SWI_start_interrupt);
  and and_3 (and_3_out, or_1_out, not_2_out);
  not not_2 (not_2_out, return_from_interrupt_1_return_from_interrupt);
  or or_2 (or_2_out, K2_Interrupt, K1_Interrupt);
  S_R_Flip_Flop s_r_ff_1 (
    .S(and_3_out), .clk(CLOCK), .R(return_from_interrupt_1_return_from_interrupt), .Q(s_r_ff_1_q), .en(1'b1));  // open: Qn, preset, reset
  Multiplexer #(.width(16)) multiplexer_3 (
    .in0(OpCode), .in1(multiplexer_1_out), .out(multiplexer_3_out), .sel(and_4_out));  // open: en
  and and_4 (and_4_out, or_2_out, not_3_out);
  not not_3 (not_3_out, return_from_interrupt_1_return_from_interrupt);
  Multiplexer #(.width(16)) multiplexer_4 (
    .in0(multiplexer_3_out), .in1(OpCode), .out(New_Opcode), .sel(s_r_ff_1_q));  // open: en

  // Notes on the sheet:
  //   Remember which interrupt we ran last
  //   RTI
  //   Problem: when we return from interrupt, this latch stays on so it doesn't stop and then start the next immediate interrupt
endmodule

module Shadow_Registers (
  input  [15:0] Set_Value,
  input  CLOCK,
  input  [15:0] OpCode,
  input  EN,
  output [15:0] Output_Value
);

  wire and_1_out, not_1_out, or_1_out, or_2_out, return_from_interrupt_1_return_from_interrupt, s_r_ff_1_q,
       SWI_start_interrupt;
  wire [15:0] multiplexer_1_out, register_1_q, register_2_q;

  Start_Interrupt SWI (.Op_Code(OpCode), .Start_Interrupt(SWI_start_interrupt));
  Return_from_Interrupt return_from_interrupt_1 (
    .Op_Code(OpCode), .Return_From_Interrupt(return_from_interrupt_1_return_from_interrupt));
  S_R_Flip_Flop s_r_ff_1 (
    .S(SWI_start_interrupt), .clk(CLOCK), .R(return_from_interrupt_1_return_from_interrupt), .Q(s_r_ff_1_q),
    .en(1'b1));  // open: Qn, preset, reset
  Multiplexer #(.width(16)) multiplexer_1 (
    .in0(Set_Value), .in1(register_2_q), .out(multiplexer_1_out),
    .sel(return_from_interrupt_1_return_from_interrupt));  // open: en
  or or_1 (or_1_out, SWI_start_interrupt, s_r_ff_1_q);
  not not_1 (not_1_out, or_1_out);
  or or_2 (or_2_out, return_from_interrupt_1_return_from_interrupt, EN);
  Register #(.width(16)) register_1 (.D(multiplexer_1_out), .en(or_2_out), .Q(register_1_q), .clk(CLOCK));  // open: clr
  and and_1 (and_1_out, not_1_out, or_2_out);
  Register #(.width(16)) register_2 (
    .D(multiplexer_1_out), .en(and_1_out), .Q(register_2_q), .clk(CLOCK));  // open: clr
  Multiplexer #(.width(16)) multiplexer_2 (
    .in0(register_2_q), .in1(register_1_q), .out(Output_Value), .sel(or_1_out));  // open: en

  // Notes on the sheet:
  //   RTI
  //   Enable Register File?
endmodule

module Shadow_PC (
  input  [15:0] Set_Value,
  input  CLOCK,
  input  [15:0] OpCode,
  input  EN,
  output [15:0] Output_Value
);

  wire and_1_out, not_1_out, not_2_out, or_1_out, return_from_interrupt_1_return_from_interrupt, s_r_ff_1_q,
       SWI_start_interrupt;
  wire [15:0] multiplexer_1_out, register_1_q, register_2_q;

  Start_Interrupt SWI (.Op_Code(OpCode), .Start_Interrupt(SWI_start_interrupt));
  Return_from_Interrupt return_from_interrupt_1 (
    .Op_Code(OpCode), .Return_From_Interrupt(return_from_interrupt_1_return_from_interrupt));
  S_R_Flip_Flop s_r_ff_1 (
    .S(SWI_start_interrupt), .clk(CLOCK), .R(return_from_interrupt_1_return_from_interrupt), .Q(s_r_ff_1_q),
    .en(1'b1));  // open: Qn, preset, reset
  Multiplexer #(.width(16)) multiplexer_1 (
    .in0(Set_Value), .in1(register_2_q), .out(multiplexer_1_out),
    .sel(return_from_interrupt_1_return_from_interrupt));  // open: en
  not not_1 (not_1_out, SWI_start_interrupt);
  not not_2 (not_2_out, s_r_ff_1_q);
  or or_1 (or_1_out, return_from_interrupt_1_return_from_interrupt, EN);
  Register #(.width(16)) register_1 (.D(multiplexer_1_out), .en(or_1_out), .Q(register_1_q), .clk(CLOCK));  // open: clr
  and and_1 (and_1_out, not_1_out, not_2_out, or_1_out);
  Register #(.width(16), .trigger("falling")) register_2 (
    .D(multiplexer_1_out), .en(and_1_out), .Q(register_2_q), .clk(CLOCK));  // open: clr
  Multiplexer #(.width(16)) multiplexer_2 (
    .in0(register_2_q), .in1(register_1_q), .out(Output_Value), .sel(s_r_ff_1_q));  // open: en

  // Notes on the sheet:
  //   RTI
  //   Enable Register File?
  //   this was falling edge so the shadow register can correctly save the PC 
  //   otherwise, pc gets NEXT value rather than current
  //   Maybe this can't be on the falling edge
endmodule

module Shadow_Flags (
  input  [4:0] Set_Flags,
  input  Clock,
  input  [15:0] OpCode,
  output [4:0] Output_Flags
);

  wire and_1_out, disable_flags_1_enable___1__disable___0, not_1_out, or_1_out,
       return_from_interrupt_1_return_from_interrupt, s_r_ff_1_q, SWI_start_interrupt;
  wire [4:0] multiplexer_1_out, register_1_q, register_2_q;

  Start_Interrupt SWI (.Op_Code(OpCode), .Start_Interrupt(SWI_start_interrupt));
  Return_from_Interrupt return_from_interrupt_1 (
    .Op_Code(OpCode), .Return_From_Interrupt(return_from_interrupt_1_return_from_interrupt));
  Disable_Flags disable_flags_1 (.Op_Code(OpCode), .Enable___1__Disable___0(disable_flags_1_enable___1__disable___0));
  S_R_Flip_Flop s_r_ff_1 (
    .S(SWI_start_interrupt), .clk(Clock), .R(return_from_interrupt_1_return_from_interrupt), .Q(s_r_ff_1_q),
    .en(1'b1));  // open: Qn, preset, reset
  Multiplexer #(.width(5)) multiplexer_1 (
    .in0(Set_Flags), .in1(register_2_q), .out(multiplexer_1_out),
    .sel(return_from_interrupt_1_return_from_interrupt));  // open: en
  not not_1 (not_1_out, s_r_ff_1_q);
  or or_1 (or_1_out, return_from_interrupt_1_return_from_interrupt, disable_flags_1_enable___1__disable___0);
  Register #(.width(5)) register_1 (.D(multiplexer_1_out), .en(or_1_out), .Q(register_1_q), .clk(Clock));  // open: clr
  and and_1 (and_1_out, not_1_out, or_1_out);
  Register #(.width(5)) register_2 (.D(multiplexer_1_out), .en(and_1_out), .Q(register_2_q), .clk(Clock));  // open: clr
  Multiplexer #(.width(5)) multiplexer_2 (
    .in0(register_2_q), .in1(register_1_q), .out(Output_Flags), .sel(s_r_ff_1_q));  // open: en

  // Notes on the sheet:
  //   RTI
  //   Enable Flags?
endmodule

module Start_Interrupt (
  input  [15:0] Op_Code,
  output Start_Interrupt
);

  Comparator comparator_1 (.a(Op_Code[15:8]), .b(8'h22), .eq(Start_Interrupt));  // open: gt, lt

  // Notes on the sheet:
  //   Interrupts are 0010 0010 000s/h iiii
endmodule

module Return_from_Interrupt (
  input  [15:0] Op_Code,
  output Return_From_Interrupt
);

  Comparator #(.width(16)) comparator_1 (.a(Op_Code), .b(16'h2300), .eq(Return_From_Interrupt));  // open: gt, lt

  // Notes on the sheet:
  //   RTI is 0010 0011 0000 0000
endmodule

module Branching_Control (
  input  [15:0] Op_Code,
  input  [15:0] Contents_of_Rb,
  input  [15:0] Current_Value_of_PC,
  input  [4:0] Current_Flags,
  input  CALL_RETURN,
  output [15:0] New_Value_of_PC
);

  wire and_1_out, clock_1_out, comparator_1_eq, comparator_2_eq, not_1_out, or_1_out,
       return_from_interrupt_1_return_from_interrupt, s_r_ff_1_q, SWI_start_interrupt;
  wire [3:0] bitselector_1_out, bitselector_2_out;
  wire [15:0] adder_1_out, BC_BCR_new_value_of_pc, BG_BGR_new_value_of_pc, BGE_BGER_new_value_of_pc,
       BL_BLR_new_value_of_pc, BLE_BLER_new_value_of_pc, BNC_BNCR_new_value_of_pc, BNS_BNSR_new_value_of_pc,
       BNV_BNVR_new_value_of_pc, BNZ_BNZR_new_value_of_pc, BR_BRR_new_value_of_pc, BS_BSR_new_value_of_pc,
       BUG_BUGR_new_value_of_pc, BULE_BULER_new_value_of_pc, BV_BVR_new_value_of_pc, BZ_BZR_new_value_of_pc,
       multiplexer_1_out, multiplexer_2_out, multiplexer_3_out;

  BR_BRR__Unconditional_Branch BR_BRR (
    .Op_Code(Op_Code), .Contents_of_Rb(Contents_of_Rb), .Current_Value_of_PC(Current_Value_of_PC),
    .New_Value_of_PC(BR_BRR_new_value_of_pc));
  BL_BLR BL_BLR (
    .Op_Code(Op_Code), .Contents_of_Rb(Contents_of_Rb), .Current_Value_of_PC(Current_Value_of_PC),
    .Current_Flags(Current_Flags), .New_Value_of_PC(BL_BLR_new_value_of_pc));
  BGE_BGER BGE_BGER (
    .Op_Code(Op_Code), .Contents_of_Rb(Contents_of_Rb), .Current_Value_of_PC(Current_Value_of_PC),
    .Current_Flags(Current_Flags), .New_Value_of_PC(BGE_BGER_new_value_of_pc));
  BLE_BLER BLE_BLER (
    .Op_Code(Op_Code), .Contents_of_Rb(Contents_of_Rb), .Current_Value_of_PC(Current_Value_of_PC),
    .Current_Flags(Current_Flags), .New_Value_of_PC(BLE_BLER_new_value_of_pc));
  BG_BGR BG_BGR (
    .Op_Code(Op_Code), .Contents_of_Rb(Contents_of_Rb), .Current_Value_of_PC(Current_Value_of_PC),
    .Current_Flags(Current_Flags), .New_Value_of_PC(BG_BGR_new_value_of_pc));
  BULE_BULER BULE_BULER (
    .Op_Code(Op_Code), .Contents_of_Rb(Contents_of_Rb), .Current_Value_of_PC(Current_Value_of_PC),
    .Current_Flags(Current_Flags), .New_Value_of_PC(BULE_BULER_new_value_of_pc));
  BUG_BUGR BUG_BUGR (
    .Op_Code(Op_Code), .Contents_of_Rb(Contents_of_Rb), .Current_Value_of_PC(Current_Value_of_PC),
    .Current_Flags(Current_Flags), .New_Value_of_PC(BUG_BUGR_new_value_of_pc));
  BZ_BZR BZ_BZR (
    .Op_Code(Op_Code), .Contents_of_Rb(Contents_of_Rb), .Current_Value_of_PC(Current_Value_of_PC),
    .Current_Flags(Current_Flags), .New_Value_of_PC(BZ_BZR_new_value_of_pc));
  BNZ_BNZR BNZ_BNZR (
    .Op_Code(Op_Code), .Contents_of_Rb(Contents_of_Rb), .Current_Value_of_PC(Current_Value_of_PC),
    .Current_Flags(Current_Flags), .New_Value_of_PC(BNZ_BNZR_new_value_of_pc));
  BC_BCR BC_BCR (
    .Op_Code(Op_Code), .Contents_of_Rb(Contents_of_Rb), .Current_Value_of_PC(Current_Value_of_PC),
    .Current_Flags(Current_Flags), .New_Value_of_PC(BC_BCR_new_value_of_pc));
  BNC_BNCR BNC_BNCR (
    .Op_Code(Op_Code), .Contents_of_Rb(Contents_of_Rb), .Current_Value_of_PC(Current_Value_of_PC),
    .Current_Flags(Current_Flags), .New_Value_of_PC(BNC_BNCR_new_value_of_pc));
  BS_BSR BS_BSR (
    .Op_Code(Op_Code), .Contents_of_Rb(Contents_of_Rb), .Current_Value_of_PC(Current_Value_of_PC),
    .Current_Flags(Current_Flags), .New_Value_of_PC(BS_BSR_new_value_of_pc));
  BNS_BNSR BNS_BNSR (
    .Op_Code(Op_Code), .Contents_of_Rb(Contents_of_Rb), .Current_Value_of_PC(Current_Value_of_PC),
    .Current_Flags(Current_Flags), .New_Value_of_PC(BNS_BNSR_new_value_of_pc));
  BV_BVR BV_BVR (
    .Op_Code(Op_Code), .Contents_of_Rb(Contents_of_Rb), .Current_Value_of_PC(Current_Value_of_PC),
    .Current_Flags(Current_Flags), .New_Value_of_PC(BV_BVR_new_value_of_pc));
  BNV_BNVR BNV_BNVR (
    .Op_Code(Op_Code), .Contents_of_Rb(Contents_of_Rb), .Current_Value_of_PC(Current_Value_of_PC),
    .Current_Flags(Current_Flags), .New_Value_of_PC(BNV_BNVR_new_value_of_pc));
  BitSelector #(.width(16), .group(4)) bitselector_1 (.in(Op_Code), .out(bitselector_1_out), .sel(2'b10));
  Multiplexer #(.select(4), .width(16)) multiplexer_1 (
    .in0(BR_BRR_new_value_of_pc), .in2(BL_BLR_new_value_of_pc), .in3(BGE_BGER_new_value_of_pc),
    .in4(BLE_BLER_new_value_of_pc), .in5(BG_BGR_new_value_of_pc), .in6(BULE_BULER_new_value_of_pc),
    .in7(BUG_BUGR_new_value_of_pc), .in8(BZ_BZR_new_value_of_pc), .in9(BNZ_BNZR_new_value_of_pc),
    .in10(BC_BCR_new_value_of_pc), .in11(BNC_BNCR_new_value_of_pc), .in12(BS_BSR_new_value_of_pc),
    .in13(BNS_BNSR_new_value_of_pc), .in14(BV_BVR_new_value_of_pc), .in15(BNV_BNVR_new_value_of_pc),
    .out(multiplexer_1_out), .sel(bitselector_1_out));  // open: in1, en
  BitSelector #(.width(16), .group(4)) bitselector_2 (.in(Op_Code), .out(bitselector_2_out), .sel(2'b11));
  Comparator #(.width(4)) comparator_1 (.a(bitselector_2_out), .b(4'b0000), .eq(comparator_1_eq));  // open: gt, lt
  Comparator #(.width(4)) comparator_2 (.a(bitselector_2_out), .b(4'b0001), .eq(comparator_2_eq));  // open: gt, lt
  Adder #(.width(16)) adder_1 (.a(Current_Value_of_PC), .b(16'h1), .out(adder_1_out));  // open: cin, cout
  or or_1 (or_1_out, comparator_1_eq, comparator_2_eq);
  Multiplexer #(.width(16)) multiplexer_2 (
    .in0(adder_1_out), .in1(multiplexer_1_out), .out(multiplexer_2_out), .sel(or_1_out));  // open: en
  Start_Interrupt SWI (.Op_Code(Op_Code), .Start_Interrupt(SWI_start_interrupt));
  Return_from_Interrupt return_from_interrupt_1 (
    .Op_Code(Op_Code), .Return_From_Interrupt(return_from_interrupt_1_return_from_interrupt));
  Multiplexer #(.width(16)) multiplexer_3 (
    .in0(multiplexer_2_out), .in1(Contents_of_Rb), .out(multiplexer_3_out), .sel(CALL_RETURN));  // open: en
  Clock clock_1 (.out(clock_1_out));
  Multiplexer #(.width(16)) multiplexer_4 (
    .in0(multiplexer_3_out), .in1(16'h3), .out(New_Value_of_PC), .sel(and_1_out));  // open: en
  and and_1 (and_1_out, SWI_start_interrupt, not_1_out);
  not not_1 (not_1_out, s_r_ff_1_q);
  S_R_Flip_Flop s_r_ff_1 (
    .S(SWI_start_interrupt), .clk(clock_1_out), .R(return_from_interrupt_1_return_from_interrupt),
    .Q(s_r_ff_1_q), .en(1'b1));  // open: Qn, preset, reset

  // Notes on the sheet:
  //   Flag Conditions
  //   Branch or not?
  //   Otherwise, PC = PC+1
  //   RTI
  //   Call/Return?
  //   Interrupt PC Value
endmodule

module Op_Control (
  input  [15:0] Op_Code,
  output _1___Current_line_is_HALT,
  output [3:0] Destination_Address__always_bits_8_11___if_Getchar__make_it_bits_0_3,
  output [3:0] Operand_1_Address__bits_4_7_if_arithmetic_bitwise_call_return__Destination_Address_otherwise,
  output [3:0] Operand_2_Address__always_bits_0_3,
  output Op_Select,
  output Enable_Disable_Register_File,
  output Enable_Disable_Flags,
  output Flag_Manipulation,
  output STORE_Operation,
  output LOAD_Operation,
  output CALL_RETURN_Operation,
  output Putchar_Operation,
  output Getchar_Operation
);

  wire getchar_operation_1_getchar_op;
  wire [3:0] bitselector_1_out, bitselector_2_out, bitselector_3_out;

  BitSelector #(.width(16), .group(4)) bitselector_1 (.in(Op_Code), .out(bitselector_1_out), .sel(2'b10));
  BitSelector #(.width(16), .group(4)) bitselector_2 (.in(Op_Code), .out(bitselector_2_out), .sel(2'b01));
  BitSelector #(.width(16), .group(4)) bitselector_3 (.in(Op_Code), .out(bitselector_3_out), .sel(2'b11));
  BitSelector #(.width(16), .group(4)) bitselector_4 (
    .in(Op_Code), .out(Operand_2_Address__always_bits_0_3), .sel(2'b00));
  Op_Select op_select_1 (.Op_Code(Op_Code), .Type_of_Operation(Op_Select));
  Disable_Register_File disable_register_file_1 (
    .Op_Code(Op_Code), .Enable___1__Disable___0(Enable_Disable_Register_File));
  Disable_Flags disable_flags_1 (.Op_Code(Op_Code), .Enable___1__Disable___0(Enable_Disable_Flags));
  Flag_Manipulation flag_manipulation_1 (.Op_Code(Op_Code), .Flag_Manipulation(Flag_Manipulation));
  STORE_Operation store_operation_1 (.Op_Code(Op_Code), .STORE_Operation(STORE_Operation));
  LOAD_Operation load_operation_1 (.Op_Code(Op_Code), .LOAD_Operation(LOAD_Operation));
  CALL_RETURN_Op call_return_op_1 (.Op_Code(Op_Code), .CALL_RETURN_Operation(CALL_RETURN_Operation));
  Getchar_Operation getchar_operation_1 (.Op_Code(Op_Code), .Getchar_op(getchar_operation_1_getchar_op));
  Putchar_Operation putchar_operation_1 (.Op_Code(Op_Code), .Putchar_op(Putchar_Operation));
  Getchar_Operation getchar_operation_2 (.Op_Code(Op_Code), .Getchar_op(Getchar_Operation));
  Multiplexer #(.select(4), .width(4)) multiplexer_1 (
    .in0(bitselector_1_out), .in1(bitselector_1_out), .in2(bitselector_2_out), .in3(bitselector_1_out),
    .in4(bitselector_1_out), .in5(bitselector_1_out), .in6(bitselector_1_out), .in7(bitselector_1_out),
    .in8(bitselector_2_out), .in9(bitselector_2_out), .in10(bitselector_2_out), .in11(bitselector_2_out),
    .in12(bitselector_2_out), .in13(bitselector_2_out), .in14(bitselector_1_out), .in15(bitselector_1_out),
    .out(Operand_1_Address__bits_4_7_if_arithmetic_bitwise_call_return__Destination_Address_otherwise),
    .sel(bitselector_3_out));  // open: en
  Comparator #(.width(16)) comparator_1 (.a(Op_Code), .b({16{1'b0}}), .eq(_1___Current_line_is_HALT));  // open: gt, lt
  Multiplexer #(.width(4)) multiplexer_2 (
    .in0(bitselector_1_out), .in1(Operand_2_Address__always_bits_0_3),
    .out(Destination_Address__always_bits_8_11___if_Getchar__make_it_bits_0_3),
    .sel(getchar_operation_1_getchar_op));  // open: en

  // Notes on the sheet:
  //   HALT Line ?
  //   DESTINATION Address (always bits 8-11)
  //   Disable the Flags (Control Flow)?
  //   Selects the type of operation (Set/Inc/Dec, or Arith/Bit/Shift?)
  //   Disable the Register File (Flag Manipulation/Memory/Control Flow)?
  //   SOURCE Addresses
  //   For putchar_ord, this will be 0001 (R1 tells us which terminal to print to)
  //   For putchar_ord, this will be 0010 (R2 holds the character we will print)
endmodule

module Op_Select (
  input  [15:0] Op_Code,
  output Type_of_Operation
);

  wire bitselector_1_out, bitselector_3_out, comparator_1_eq, comparator_2_eq, or_1_out;
  wire [3:0] bitselector_2_out;

  BitSelector #(.width(16)) bitselector_1 (.in(Op_Code), .out(bitselector_1_out), .sel(4'b0111));
  BitSelector #(.width(16), .group(4)) bitselector_2 (.in(Op_Code), .out(bitselector_2_out), .sel(2'b11));
  BitSelector #(.width(4)) bitselector_3 (.in(bitselector_2_out), .out(bitselector_3_out), .sel(2'b11));
  Comparator #(.width(4)) comparator_1 (.a(bitselector_2_out), .b(4'b1111), .eq(comparator_1_eq));  // open: gt, lt
  Comparator #(.width(4)) comparator_2 (.a(bitselector_2_out), .b(4'b1110), .eq(comparator_2_eq));  // open: gt, lt
  or or_1 (or_1_out, comparator_1_eq, comparator_2_eq);
  Multiplexer multiplexer_1 (
    .in0(bitselector_1_out), .in1(or_1_out), .out(Type_of_Operation), .sel(bitselector_3_out));  // open: en

  // Notes on the sheet:
  //   Bit 7
  //   Bits 12-15
  //   Bit 15
  //   Set: 1110 or 1111
  //   Set, Inc, or Dec Operation?
  //   Arith, Bit, or Shift Operation?
  //   Set/Inc/Dec, or Arith/Bit/Shift Operation?
endmodule

module ALSU (
  input  [15:0] Operand_1,
  input  [15:0] Operand_2,
  input  [4:0] Current_Flags,
  input  [15:0] Op_Code,
  input  Op_Select,
  input  [15:0] GetChar_Data,
  output [4:0] Final_Updated_Flags,
  output [15:0] Final_Result__could_be_Getchar_data
);

  wire getchar_operation_1_getchar_op;
  wire [4:0] Arith___Bit___Shift_arith_bit_shift_updated_flags, Set___Inc___Dec_set_inc_dec_updated_flags;
  wire [15:0] Arith___Bit___Shift_arith_bit_shift_result, multiplexer_1_out,
       Set___Inc___Dec_set_inc_dec_result;

  Getchar_Operation getchar_operation_1 (.Op_Code(Op_Code), .Getchar_op(getchar_operation_1_getchar_op));
  Arith_Bit_Shift Arith___Bit___Shift (
    .Arith_Bit_Shift_Updated_Flags(Arith___Bit___Shift_arith_bit_shift_updated_flags), .Operand_1(Operand_1),
    .Operand_2(Operand_2), .Arith_Bit_Shift_Result(Arith___Bit___Shift_arith_bit_shift_result),
    .Current_Flags(Current_Flags), .Op_Code(Op_Code));
  Set_Inc_Decr Set___Inc___Dec (
    .Operand_1(Operand_1), .Operand_2(Operand_2), .Current_Flags(Current_Flags), .Op_Code(Op_Code),
    .Set_Inc_Dec_Result(Set___Inc___Dec_set_inc_dec_result),
    .Set_Inc_Dec_Updated_Flags(Set___Inc___Dec_set_inc_dec_updated_flags));
  Multiplexer #(.width(16)) multiplexer_1 (
    .in0(Arith___Bit___Shift_arith_bit_shift_result), .in1(Set___Inc___Dec_set_inc_dec_result),
    .out(multiplexer_1_out), .sel(Op_Select));  // open: en
  Multiplexer #(.width(5)) multiplexer_2 (
    .in0(Arith___Bit___Shift_arith_bit_shift_updated_flags), .in1(Set___Inc___Dec_set_inc_dec_updated_flags),
    .out(Final_Updated_Flags), .sel(Op_Select));  // open: en
  Multiplexer #(.width(16)) multiplexer_3 (
    .in0(multiplexer_1_out), .in1(GetChar_Data), .out(Final_Result__could_be_Getchar_data),
    .sel(getchar_operation_1_getchar_op));  // open: en
endmodule

module Flags (
  input  [4:0] Current_Flags__from_ALSU,
  input  [4:0] Current_Flags__from_Manipulation,
  input  [4:0] Current_Flags__from_LOAD,
  input  Flag_Manipulation,
  input  LOAD_Operation,
  input  [15:0] OpCode,
  output [4:0] Updated_Flags
);

  wire CLOCK_out;
  wire [4:0] multiplexer_1_out, multiplexer_2_out;

  Clock CLOCK (.out(CLOCK_out));
  Multiplexer #(.width(5)) multiplexer_1 (
    .in0(Current_Flags__from_ALSU), .in1(Current_Flags__from_Manipulation), .out(multiplexer_1_out),
    .sel(Flag_Manipulation));  // open: en
  Multiplexer #(.width(5)) multiplexer_2 (
    .in0(multiplexer_1_out), .in1(Current_Flags__from_LOAD), .out(multiplexer_2_out), .sel(LOAD_Operation));  // open: en
  Shadow_Flags shadow_flags_1 (
    .Set_Flags(multiplexer_2_out), .Clock(CLOCK_out), .OpCode(OpCode), .Output_Flags(Updated_Flags));

  // Notes on the sheet:
  //   carry block; carry; overflow; zero; sign
endmodule

module Putchar_Operation (
  input  [15:0] Op_Code,
  output Putchar_op
);

  Comparator #(.width(6)) comparator_1 (.a(Op_Code[15:10]), .b(6'b001010), .eq(Putchar_op));  // open: gt, lt

  // Notes on the sheet:
  //   Put something on screen (bits 15-10 to be 001010)
endmodule

module Getchar_Operation (
  input  [15:0] Op_Code,
  output Getchar_op
);

  Comparator #(.width(6)) comparator_1 (.a(Op_Code[15:10]), .b(6'b001011), .eq(Getchar_op));  // open: gt, lt

  // Notes on the sheet:
  //   Check if keyboard has char (bits 15-10 to be 001011)
endmodule

module Register_SubCircuit (
  input  EN1,
  input  EN2_3,
  input  Input_1,
  input  Input_2,
  input  Input_3,
  input  Input_4,
  input  Input_5,
  input  Input_6,
  input  Input_7,
  input  Input_8,
  input  Input_9,
  input  Input_10,
  input  Input_11,
  input  Input_12,
  input  Input_13,
  input  Input_14,
  input  Input_15,
  input  Input_1_2,
  input  Input_2_2,
  input  Input_3_2,
  input  Input_4_2,
  input  Input_5_2,
  input  Input_6_2,
  input  Input_7_2,
  input  Input_8_2,
  input  Input_9_2,
  input  Input_10_2,
  input  Input_11_2,
  input  Input_12_2,
  input  Input_13_2,
  input  Input_14_2,
  input  Input_15_2,
  input  Input_1_3,
  input  Input_2_3,
  input  Input_3_3,
  input  Input_4_3,
  input  Input_5_3,
  input  Input_6_3,
  input  Input_7_3,
  input  Input_8_3,
  input  Input_9_3,
  input  Input_10_3,
  input  Input_11_3,
  input  Input_12_3,
  input  Input_13_3,
  input  Input_14_3,
  input  Input_15_3,
  input  [15:0] WD1,
  input  [15:0] WD2,
  input  [15:0] WD3,
  output R1_EN,
  output R2_EN,
  output R3_EN,
  output R4_EN,
  output R5__EN,
  output R6_EN,
  output R7_EN,
  output R8_EN,
  output R9_EN,
  output R10_EN,
  output R11_EN,
  output R12_EN,
  output R13_EN,
  output R14_EN,
  output R15_EN,
  output [15:0] R1_WD,
  output [15:0] R2_WD,
  output [15:0] R3_WD,
  output [15:0] R4_WD,
  output [15:0] R5_WD,
  output [15:0] R6_WD,
  output [15:0] R7_WD,
  output [15:0] R8_WD,
  output [15:0] R9_WD,
  output [15:0] R10_WD,
  output [15:0] R11_WD,
  output [15:0] R12_WD,
  output [15:0] R13_WD,
  output [15:0] R14_WD,
  output [15:0] R15_WD
);

  wire and_1_out, and_2_out, and_3_out, and_4_out, and_5_out, and_6_out, and_7_out, and_8_out, and_9_out,
       and_10_out, and_11_out, and_12_out, and_13_out, and_14_out, and_15_out, and_16_out, and_17_out,
       and_18_out, and_19_out, and_20_out, and_21_out, and_22_out, and_23_out, and_24_out, and_25_out,
       and_26_out, and_27_out, and_28_out, and_29_out, and_30_out, and_31_out, and_32_out, and_33_out,
       and_34_out, and_35_out, and_36_out, and_37_out, and_38_out, and_39_out, and_40_out, and_41_out,
       and_42_out, and_43_out, and_44_out, and_45_out;
  wire [15:0] multiplexer_1_out, multiplexer_2_out, multiplexer_3_out, multiplexer_4_out, multiplexer_5_out,
       multiplexer_6_out, multiplexer_7_out, multiplexer_8_out, multiplexer_9_out, multiplexer_10_out,
       multiplexer_11_out, multiplexer_12_out, multiplexer_13_out, multiplexer_14_out, multiplexer_15_out,
       multiplexer_16_out, multiplexer_17_out, multiplexer_18_out, multiplexer_19_out, multiplexer_20_out,
       multiplexer_21_out, multiplexer_22_out, multiplexer_23_out, multiplexer_24_out, multiplexer_25_out,
       multiplexer_26_out, multiplexer_27_out, multiplexer_28_out, multiplexer_29_out, multiplexer_30_out,
       multiplexer_31_out, multiplexer_32_out, multiplexer_33_out, multiplexer_34_out, multiplexer_35_out,
       multiplexer_36_out, multiplexer_37_out, multiplexer_38_out, multiplexer_39_out, multiplexer_40_out,
       multiplexer_41_out, multiplexer_42_out, multiplexer_43_out, multiplexer_44_out, multiplexer_45_out;

  Multiplexer #(.width(16)) multiplexer_1 (
    .in0({16{1'b0}}), .in1(WD1), .out(multiplexer_1_out), .sel(and_25_out));  // open: en
  and and_1 (and_1_out, EN1, Input_9);
  and and_2 (and_2_out, EN2_3, Input_9_2);
  and and_3 (and_3_out, EN2_3, Input_9_3);
  Multiplexer #(.width(16)) multiplexer_2 (
    .in0({16{1'b0}}), .in1(WD1), .out(multiplexer_2_out), .sel(and_1_out));  // open: en
  Multiplexer #(.width(16)) multiplexer_3 (
    .in0({16{1'b0}}), .in1(WD1), .out(multiplexer_3_out), .sel(and_7_out));  // open: en
  Multiplexer #(.width(16)) multiplexer_4 (
    .in0({16{1'b0}}), .in1(WD1), .out(multiplexer_4_out), .sel(and_34_out));  // open: en
  Multiplexer #(.width(16)) multiplexer_5 (
    .in0({16{1'b0}}), .in1(WD2), .out(multiplexer_5_out), .sel(and_35_out));  // open: en
  Multiplexer #(.width(16)) multiplexer_6 (
    .in0({16{1'b0}}), .in1(WD3), .out(multiplexer_6_out), .sel(and_27_out));  // open: en
  Multiplexer #(.width(16)) multiplexer_7 (
    .in0({16{1'b0}}), .in1(WD2), .out(multiplexer_7_out), .sel(and_26_out));  // open: en
  or or_1 (R9_EN, and_1_out, and_2_out, and_3_out);
  Multiplexer #(.width(16)) multiplexer_8 (
    .in0({16{1'b0}}), .in1(WD2), .out(multiplexer_8_out), .sel(and_2_out));  // open: en
  Multiplexer #(.width(16)) multiplexer_9 (
    .in0({16{1'b0}}), .in1(WD3), .out(multiplexer_9_out), .sel(and_9_out));  // open: en
  Multiplexer #(.width(16)) multiplexer_10 (
    .in0({16{1'b0}}), .in1(WD2), .out(multiplexer_10_out), .sel(and_8_out));  // open: en
  Multiplexer #(.width(16)) multiplexer_11 (
    .in0({16{1'b0}}), .in1(WD3), .out(multiplexer_11_out), .sel(and_36_out));  // open: en
  assign R12_WD = multiplexer_6_out | multiplexer_7_out | multiplexer_1_out;  // OR_Gate or_2, 16 bits wide
  and and_4 (and_4_out, EN1, Input_1);
  and and_5 (and_5_out, Input_1_2, EN2_3);
  and and_6 (and_6_out, EN2_3, Input_1_3);
  Multiplexer #(.width(16)) multiplexer_12 (
    .in0({16{1'b0}}), .in1(WD3), .out(multiplexer_12_out), .sel(and_3_out));  // open: en
  assign R2_WD = multiplexer_9_out | multiplexer_10_out | multiplexer_3_out;  // OR_Gate or_3, 16 bits wide
  assign R7_WD = multiplexer_11_out | multiplexer_5_out | multiplexer_4_out;  // OR_Gate or_4, 16 bits wide
  or or_5 (R1_EN, and_4_out, and_5_out, and_6_out);
  and and_7 (and_7_out, EN1, Input_2);
  and and_8 (and_8_out, Input_2_2, EN2_3);
  and and_9 (and_9_out, EN2_3, Input_2_3);
  and and_10 (and_10_out, EN1, Input_10);
  and and_11 (and_11_out, EN2_3, Input_10_2);
  and and_12 (and_12_out, Input_10_3, EN2_3);
  assign R9_WD = multiplexer_12_out | multiplexer_8_out | multiplexer_2_out;  // OR_Gate or_6, 16 bits wide
  Multiplexer #(.width(16)) multiplexer_13 (
    .in0({16{1'b0}}), .in1(WD1), .out(multiplexer_13_out), .sel(and_28_out));  // open: en
  or or_7 (R2_EN, and_7_out, and_8_out, and_9_out);
  and and_13 (and_13_out, EN1, Input_3);
  and and_14 (and_14_out, EN2_3, Input_3_2);
  and and_15 (and_15_out, EN2_3, Input_3_3);
  or or_8 (R10_EN, and_10_out, and_12_out, and_11_out);
  and and_16 (and_16_out, EN1, Input_11);
  and and_17 (and_17_out, Input_11_2, EN2_3);
  and and_18 (and_18_out, EN2_3, Input_11_3);
  Multiplexer #(.width(16)) multiplexer_14 (
    .in0({16{1'b0}}), .in1(WD1), .out(multiplexer_14_out), .sel(and_4_out));  // open: en
  Multiplexer #(.width(16)) multiplexer_15 (
    .in0({16{1'b0}}), .in1(WD1), .out(multiplexer_15_out), .sel(and_19_out));  // open: en
  Multiplexer #(.width(16)) multiplexer_16 (
    .in0({16{1'b0}}), .in1(WD2), .out(multiplexer_16_out), .sel(and_29_out));  // open: en
  or or_9 (R3_EN, and_13_out, and_14_out, and_15_out);
  or or_10 (R11_EN, and_16_out, and_17_out, and_18_out);
  Multiplexer #(.width(16)) multiplexer_17 (
    .in0({16{1'b0}}), .in1(WD2), .out(multiplexer_17_out), .sel(and_5_out));  // open: en
  Multiplexer #(.width(16)) multiplexer_18 (
    .in0({16{1'b0}}), .in1(WD2), .out(multiplexer_18_out), .sel(and_20_out));  // open: en
  Multiplexer #(.width(16)) multiplexer_19 (
    .in0({16{1'b0}}), .in1(WD1), .out(multiplexer_19_out), .sel(and_40_out));  // open: en
  Multiplexer #(.width(16)) multiplexer_20 (
    .in0({16{1'b0}}), .in1(WD2), .out(multiplexer_20_out), .sel(and_41_out));  // open: en
  Multiplexer #(.width(16)) multiplexer_21 (
    .in0({16{1'b0}}), .in1(WD3), .out(multiplexer_21_out), .sel(and_30_out));  // open: en
  assign R13_WD = multiplexer_21_out | multiplexer_16_out | multiplexer_13_out;  // OR_Gate or_11, 16 bits wide
  and and_19 (and_19_out, EN1, Input_4);
  and and_20 (and_20_out, EN2_3, Input_4_2);
  and and_21 (and_21_out, Input_4_3, EN2_3);
  Multiplexer #(.width(16)) multiplexer_22 (
    .in0({16{1'b0}}), .in1(WD3), .out(multiplexer_22_out), .sel(and_6_out));  // open: en
  assign R1_WD = multiplexer_22_out | multiplexer_17_out | multiplexer_14_out;  // OR_Gate or_12, 16 bits wide
  Multiplexer #(.width(16)) multiplexer_23 (
    .in0({16{1'b0}}), .in1(WD3), .out(multiplexer_23_out), .sel(and_21_out));  // open: en
  Multiplexer #(.width(16)) multiplexer_24 (
    .in0({16{1'b0}}), .in1(WD3), .out(multiplexer_24_out), .sel(and_42_out));  // open: en
  or or_13 (R4_EN, and_19_out, and_20_out, and_21_out);
  and and_22 (and_22_out, EN1, Input_5);
  and and_23 (and_23_out, EN2_3, Input_5_2);
  and and_24 (and_24_out, EN2_3, Input_5_3);
  and and_25 (and_25_out, Input_12, EN1);
  or or_14 (R12_EN, and_25_out, and_26_out, and_27_out);
  and and_26 (and_26_out, EN2_3, Input_12_2);
  and and_27 (and_27_out, Input_12_3, Input_12_3, EN2_3);
  assign R4_WD = multiplexer_23_out | multiplexer_18_out | multiplexer_15_out;  // OR_Gate or_15, 16 bits wide
  assign R8_WD = multiplexer_24_out | multiplexer_20_out | multiplexer_19_out;  // OR_Gate or_16, 16 bits wide
  or or_17 (R5__EN, and_22_out, and_23_out, and_24_out);
  and and_28 (and_28_out, EN1, Input_13);
  or or_18 (R13_EN, and_28_out, and_29_out, and_30_out);
  and and_29 (and_29_out, EN2_3, Input_13_2);
  and and_30 (and_30_out, EN2_3, Input_13_3);
  Multiplexer #(.width(16)) multiplexer_25 (
    .in0({16{1'b0}}), .in1(WD1), .out(multiplexer_25_out), .sel(and_13_out));  // open: en
  Multiplexer #(.width(16)) multiplexer_26 (
    .in0({16{1'b0}}), .in1(WD1), .out(multiplexer_26_out), .sel(and_37_out));  // open: en
  and and_31 (and_31_out, EN1, Input_6);
  and and_32 (and_32_out, Input_6_2, EN2_3);
  and and_33 (and_33_out, EN2_3, Input_6_3);
  Multiplexer #(.width(16)) multiplexer_27 (
    .in0({16{1'b0}}), .in1(WD2), .out(multiplexer_27_out), .sel(and_14_out));  // open: en
  Multiplexer #(.width(16)) multiplexer_28 (
    .in0({16{1'b0}}), .in1(WD2), .out(multiplexer_28_out), .sel(and_23_out));  // open: en
  Multiplexer #(.width(16)) multiplexer_29 (
    .in0({16{1'b0}}), .in1(WD1), .out(multiplexer_29_out), .sel(and_22_out));  // open: en
  Multiplexer #(.width(16)) multiplexer_30 (
    .in0({16{1'b0}}), .in1(WD1), .out(multiplexer_30_out), .sel(and_10_out));  // open: en
  Multiplexer #(.width(16)) multiplexer_31 (
    .in0({16{1'b0}}), .in1(WD3), .out(multiplexer_31_out), .sel(and_39_out));  // open: en
  Multiplexer #(.width(16)) multiplexer_32 (
    .in0({16{1'b0}}), .in1(WD2), .out(multiplexer_32_out), .sel(and_38_out));  // open: en
  or or_19 (R6_EN, and_31_out, and_32_out, and_33_out);
  and and_34 (and_34_out, EN1, Input_7);
  and and_35 (and_35_out, EN2_3, Input_7_2);
  and and_36 (and_36_out, EN2_3, Input_7_3);
  and and_37 (and_37_out, EN1, Input_14);
  and and_38 (and_38_out, Input_14_2, EN2_3);
  and and_39 (and_39_out, Input_14_3, EN2_3);
  Multiplexer #(.width(16)) multiplexer_33 (
    .in0({16{1'b0}}), .in1(WD3), .out(multiplexer_33_out), .sel(and_15_out));  // open: en
  Multiplexer #(.width(16)) multiplexer_34 (
    .in0({16{1'b0}}), .in1(WD3), .out(multiplexer_34_out), .sel(and_24_out));  // open: en
  Multiplexer #(.width(16)) multiplexer_35 (
    .in0({16{1'b0}}), .in1(WD2), .out(multiplexer_35_out), .sel(and_11_out));  // open: en
  assign R14_WD = multiplexer_31_out | multiplexer_32_out | multiplexer_26_out;  // OR_Gate or_20, 16 bits wide
  or or_21 (R7_EN, and_34_out, and_35_out, and_36_out);
  or or_22 (R14_EN, and_37_out, and_38_out, and_39_out);
  assign R3_WD = multiplexer_33_out | multiplexer_27_out | multiplexer_25_out;  // OR_Gate or_23, 16 bits wide
  assign R5_WD = multiplexer_34_out | multiplexer_28_out | multiplexer_29_out;  // OR_Gate or_24, 16 bits wide
  Multiplexer #(.width(16)) multiplexer_36 (
    .in0({16{1'b0}}), .in1(WD3), .out(multiplexer_36_out), .sel(and_12_out));  // open: en
  assign R10_WD = multiplexer_36_out | multiplexer_35_out | multiplexer_30_out;  // OR_Gate or_25, 16 bits wide
  and and_40 (and_40_out, EN1, Input_8);
  and and_41 (and_41_out, Input_8_2, EN2_3);
  and and_42 (and_42_out, Input_8_3, EN2_3);
  and and_43 (and_43_out, EN1, Input_15);
  and and_44 (and_44_out, Input_15_2, EN2_3);
  and and_45 (and_45_out, Input_15_3, EN2_3);
  or or_26 (R8_EN, and_40_out, and_41_out, and_42_out);
  or or_27 (R15_EN, and_43_out, and_44_out, and_45_out);
  Multiplexer #(.width(16)) multiplexer_37 (
    .in0({16{1'b0}}), .in1(WD1), .out(multiplexer_37_out), .sel(and_43_out));  // open: en
  Multiplexer #(.width(16)) multiplexer_38 (
    .in0({16{1'b0}}), .in1(WD2), .out(multiplexer_38_out), .sel(and_44_out));  // open: en
  Multiplexer #(.width(16)) multiplexer_39 (
    .in0({16{1'b0}}), .in1(WD2), .out(multiplexer_39_out), .sel(and_32_out));  // open: en
  Multiplexer #(.width(16)) multiplexer_40 (
    .in0({16{1'b0}}), .in1(WD1), .out(multiplexer_40_out), .sel(and_31_out));  // open: en
  Multiplexer #(.width(16)) multiplexer_41 (
    .in0({16{1'b0}}), .in1(WD2), .out(multiplexer_41_out), .sel(and_17_out));  // open: en
  Multiplexer #(.width(16)) multiplexer_42 (
    .in0({16{1'b0}}), .in1(WD1), .out(multiplexer_42_out), .sel(and_16_out));  // open: en
  Multiplexer #(.width(16)) multiplexer_43 (
    .in0({16{1'b0}}), .in1(WD3), .out(multiplexer_43_out), .sel(and_45_out));  // open: en
  Multiplexer #(.width(16)) multiplexer_44 (
    .in0({16{1'b0}}), .in1(WD3), .out(multiplexer_44_out), .sel(and_33_out));  // open: en
  Multiplexer #(.width(16)) multiplexer_45 (
    .in0({16{1'b0}}), .in1(WD3), .out(multiplexer_45_out), .sel(and_18_out));  // open: en
  assign R15_WD = multiplexer_43_out | multiplexer_38_out | multiplexer_37_out;  // OR_Gate or_28, 16 bits wide
  assign R6_WD = multiplexer_44_out | multiplexer_39_out | multiplexer_40_out;  // OR_Gate or_29, 16 bits wide
  assign R11_WD = multiplexer_45_out | multiplexer_41_out | multiplexer_42_out;  // OR_Gate or_30, 16 bits wide

  // Notes on the sheet:
  //   DECODER 1
  //   DECODER2
  //   DECODER 3
endmodule

module Which_Terminal (
  input  [15:0] Op_Code,
  output _1___Print_to_terminal_1__0___Term_2,
  output _1___Print_to_terminal_1__0___Term_2_2
);


  assign _1___Print_to_terminal_1__0___Term_2 = Op_Code[0];
  assign _1___Print_to_terminal_1__0___Term_2_2 = Op_Code[0];

  // Notes on the sheet:
  //   Look at bits 4-7
endmodule

module Enable_Keyboards (
  input  Getchar_op,
  input  Which_terminal,
  output EN_1,
  output EN_2
);

  wire not_1_out;

  not not_1 (not_1_out, Which_terminal);
  and and_1 (EN_1, Getchar_op, Which_terminal);
  and and_2 (EN_2, Getchar_op, not_1_out);
endmodule

module Disable_Register_File (
  input  [15:0] Op_Code,
  output Enable___1__Disable___0
);

  wire and_1_out, and_2_out, and_3_out, bitselector_3_out, bitselector_5_out, comparator_1_eq,
       comparator_2_eq, comparator_3_eq, comparator_4_eq, comparator_5_eq, comparator_6_eq, comparator_7_eq,
       comparator_8_eq, Interrupts_start_interrupt, or_1_out, or_2_out, or_3_out,
       putchar_operation_1_putchar_op;
  wire [1:0] bitselector_4_out;
  wire [3:0] bitselector_1_out, bitselector_2_out, bitselector_6_out;

  BitSelector #(.width(16), .group(4)) bitselector_1 (.in(Op_Code), .out(bitselector_1_out), .sel(2'b11));
  BitSelector #(.width(16), .group(4)) bitselector_2 (.in(Op_Code), .out(bitselector_2_out), .sel(2'b01));
  BitSelector #(.width(16)) bitselector_3 (.in(Op_Code), .out(bitselector_3_out), .sel(4'b0011));
  BitSelector #(.width(16), .group(2)) bitselector_4 (.in(Op_Code), .out(bitselector_4_out), .sel(3'b111));
  BitSelector #(.width(16)) bitselector_5 (.in(Op_Code), .out(bitselector_5_out), .sel(4'b1101));
  BitSelector #(.width(16), .group(4)) bitselector_6 (.in(Op_Code), .out(bitselector_6_out), .sel(2'b11));
  Start_Interrupt Interrupts (.Op_Code(Op_Code), .Start_Interrupt(Interrupts_start_interrupt));
  Comparator #(.width(4)) comparator_1 (.a(bitselector_1_out), .b(4'b0011), .eq(comparator_1_eq));  // open: gt, lt
  Comparator #(.width(4)) comparator_2 (.a(bitselector_2_out), .b(4'b0110), .eq(comparator_2_eq));  // open: gt, lt
  Comparator #(.width(4)) comparator_3 (.a(bitselector_2_out), .b(4'b0111), .eq(comparator_3_eq));  // open: gt, lt
  Comparator #(.width(1)) comparator_4 (.a(bitselector_3_out), .b(1'b1), .eq(comparator_4_eq));  // open: gt, lt
  Comparator #(.width(2)) comparator_5 (.a(bitselector_4_out), .b(2'b01), .eq(comparator_5_eq));  // open: gt, lt
  Comparator #(.width(4)) comparator_6 (.a(bitselector_6_out), .b(4'b0000), .eq(comparator_6_eq));  // open: gt, lt
  Comparator #(.width(4)) comparator_7 (.a(bitselector_6_out), .b(4'b0001), .eq(comparator_7_eq));  // open: gt, lt
  Putchar_Operation putchar_operation_1 (.Op_Code(Op_Code), .Putchar_op(putchar_operation_1_putchar_op));
  Comparator #(.width(16)) comparator_8 (.a(Op_Code), .b({16{1'b0}}), .eq(comparator_8_eq));  // open: gt, lt
  or or_1 (or_1_out, comparator_2_eq, and_1_out);
  and and_1 (and_1_out, comparator_3_eq, comparator_4_eq);
  and and_2 (and_2_out, comparator_5_eq, bitselector_5_out);
  or or_2 (or_2_out, comparator_6_eq, comparator_7_eq);
  and and_3 (and_3_out, comparator_1_eq, or_1_out);
  not not_1 (Enable___1__Disable___0, or_3_out);
  or or_3 (or_3_out, comparator_8_eq, and_3_out, and_2_out, or_2_out, putchar_operation_1_putchar_op, Interrupts_start_interrupt);

  // Notes on the sheet:
  //   HALT Line ?
  //   MANIPULATING FLAGS (0011...011)
  //   STORE (011)
  //   CONTROL FLOW (00)
  //   Branches, including jumps (0001/0)
  //   Setting Flags
  //   Restoring Flags
endmodule

module Disable_Flags (
  input  [15:0] Op_Code,
  output Enable___1__Disable___0
);

  wire and_1_out, bitselector_4_out, comparator_1_eq, comparator_2_eq, comparator_3_eq, comparator_4_eq,
       comparator_5_eq, comparator_6_eq, getchar_operation_1_getchar_op, or_1_out, or_2_out, or_3_out,
       putchar_operation_1_putchar_op;
  wire [1:0] bitselector_3_out;
  wire [3:0] bitselector_1_out;
  wire [7:0] bitselector_2_out;

  BitSelector #(.width(16), .group(4)) bitselector_1 (.in(Op_Code), .out(bitselector_1_out), .sel(2'b11));
  BitSelector #(.width(16), .group(8)) bitselector_2 (.in(Op_Code), .out(bitselector_2_out), .sel(1'b1));
  BitSelector #(.width(16), .group(2)) bitselector_3 (.in(Op_Code), .out(bitselector_3_out), .sel(3'b111));
  BitSelector #(.width(16)) bitselector_4 (.in(Op_Code), .out(bitselector_4_out), .sel(4'b1101));
  Getchar_Operation getchar_operation_1 (.Op_Code(Op_Code), .Getchar_op(getchar_operation_1_getchar_op));
  Comparator #(.width(4)) comparator_1 (.a(bitselector_1_out), .b(4'b0000), .eq(comparator_1_eq));  // open: gt, lt
  Comparator #(.width(4)) comparator_2 (.a(bitselector_1_out), .b(4'b0001), .eq(comparator_2_eq));  // open: gt, lt
  Comparator comparator_3 (.a(bitselector_2_out), .b(8'h20), .eq(comparator_3_eq));  // open: gt, lt
  Comparator comparator_4 (.a(bitselector_2_out), .b(8'h21), .eq(comparator_4_eq));  // open: gt, lt
  Comparator #(.width(2)) comparator_5 (.a(bitselector_3_out), .b(2'b01), .eq(comparator_5_eq));  // open: gt, lt
  Putchar_Operation putchar_operation_1 (.Op_Code(Op_Code), .Putchar_op(putchar_operation_1_putchar_op));
  Comparator #(.width(16)) comparator_6 (.a(Op_Code), .b({16{1'b0}}), .eq(comparator_6_eq));  // open: gt, lt
  or or_1 (or_1_out, comparator_1_eq, comparator_2_eq);
  or or_2 (or_2_out, comparator_3_eq, comparator_4_eq);
  and and_1 (and_1_out, comparator_5_eq, bitselector_4_out);
  or or_3 (or_3_out, or_1_out, putchar_operation_1_putchar_op, comparator_6_eq, or_2_out, and_1_out, getchar_operation_1_getchar_op);
  not not_1 (Enable___1__Disable___0, or_3_out);

  // Notes on the sheet:
  //   HALT Line ?
  //   CONTROL FLOW (00)
  //   STORE (011)
  //   Branches, including jumps (0001/0)
  //   Function call/return (0010 000)
endmodule

module Flag_Manipulation (
  input  [15:0] Op_Code,
  output Flag_Manipulation
);

  wire and_1_out, bitselector_3_out, comparator_1_eq, comparator_2_eq, comparator_3_eq, comparator_4_eq,
       or_1_out;
  wire [3:0] bitselector_1_out, bitselector_2_out;

  BitSelector #(.width(16), .group(4)) bitselector_1 (.in(Op_Code), .out(bitselector_1_out), .sel(2'b11));
  BitSelector #(.width(16), .group(4)) bitselector_2 (.in(Op_Code), .out(bitselector_2_out), .sel(2'b01));
  BitSelector #(.width(16)) bitselector_3 (.in(Op_Code), .out(bitselector_3_out), .sel(4'b0011));
  Comparator #(.width(4)) comparator_1 (.a(bitselector_1_out), .b(4'b0011), .eq(comparator_1_eq));  // open: gt, lt
  Comparator #(.width(4)) comparator_2 (.a(bitselector_2_out), .b(4'b0110), .eq(comparator_2_eq));  // open: gt, lt
  Comparator #(.width(4)) comparator_3 (.a(bitselector_2_out), .b(4'b0111), .eq(comparator_3_eq));  // open: gt, lt
  Comparator #(.width(1)) comparator_4 (.a(bitselector_3_out), .b(1'b1), .eq(comparator_4_eq));  // open: gt, lt
  or or_1 (or_1_out, comparator_2_eq, and_1_out);
  and and_1 (and_1_out, comparator_3_eq, comparator_4_eq);
  and and_2 (Flag_Manipulation, comparator_1_eq, or_1_out);

  // Notes on the sheet:
  //   MANIPULATING FLAGS (0011...011)
  //   Setting Flags
  //   Restoring Flags
endmodule

module STORE_Operation (
  input  [15:0] Op_Code,
  output STORE_Operation
);

  wire bitselector_2_out, comparator_1_eq;
  wire [1:0] bitselector_1_out;

  BitSelector #(.width(16), .group(2)) bitselector_1 (.in(Op_Code), .out(bitselector_1_out), .sel(3'b111));
  BitSelector #(.width(16)) bitselector_2 (.in(Op_Code), .out(bitselector_2_out), .sel(4'b1101));
  Comparator #(.width(2)) comparator_1 (.a(bitselector_1_out), .b(2'b01), .eq(comparator_1_eq));  // open: gt, lt
  and and_1 (STORE_Operation, comparator_1_eq, bitselector_2_out);

  // Notes on the sheet:
  //   STORE (011)
endmodule

module LOAD_Operation (
  input  [15:0] Op_Code,
  output LOAD_Operation
);

  wire bitselector_2_out, comparator_1_eq, not_1_out;
  wire [1:0] bitselector_1_out;

  BitSelector #(.width(16), .group(2)) bitselector_1 (.in(Op_Code), .out(bitselector_1_out), .sel(3'b111));
  BitSelector #(.width(16)) bitselector_2 (.in(Op_Code), .out(bitselector_2_out), .sel(4'b1101));
  Comparator #(.width(2)) comparator_1 (.a(bitselector_1_out), .b(2'b01), .eq(comparator_1_eq));  // open: gt, lt
  not not_1 (not_1_out, bitselector_2_out);
  and and_1 (LOAD_Operation, comparator_1_eq, not_1_out);

  // Notes on the sheet:
  //   STORE (011)
endmodule

module CALL_RETURN_Op (
  input  [15:0] Op_Code,
  output CALL_RETURN_Operation
);

  wire comparator_1_eq, comparator_2_eq;
  wire [7:0] bitselector_1_out;

  BitSelector #(.width(16), .group(8)) bitselector_1 (.in(Op_Code), .out(bitselector_1_out), .sel(1'b1));
  Comparator comparator_1 (.a(bitselector_1_out), .b(8'h20), .eq(comparator_1_eq));  // open: gt, lt
  Comparator comparator_2 (.a(bitselector_1_out), .b(8'h21), .eq(comparator_2_eq));  // open: gt, lt
  or or_1 (CALL_RETURN_Operation, comparator_1_eq, comparator_2_eq);

  // Notes on the sheet:
  //   0010 0000, or 0010 0001
endmodule

module Arith_Bit_Shift (
  input  [15:0] Operand_1,
  input  [15:0] Operand_2,
  input  [4:0] Current_Flags,
  input  [15:0] Op_Code,
  output [15:0] Arith_Bit_Shift_Result,
  output [4:0] Arith_Bit_Shift_Updated_Flags
);

  wire bitselector_3_out;
  wire [3:0] bit_extender_1_out, bitselector_1_out, bitselector_2_out, or_2_out;
  wire [4:0] ADD_updated_flags, AND_updated_flags, ASL_updated_flags, ASR_updated_flags, LSL8_updated_flags,
       LSL_updated_flags, LSR8_updated_flags, LSR_updated_flags, MUL_updated_flags, multiplexer_2_out,
       OR_updated_flags, SUB_updated_flags, XOR_updated_flags;
  wire [15:0] ADD_result, AND_result, ASL_result, ASR_result, LSL8_result, LSL_result, LSR8_result,
       LSR_result, MUL_result, multiplexer_1_out, OR_result, SAVE_FLAGS_flags_saved_to_rd, SUB_result,
       XOR_result;

  AND AND (
    .Operand_1(Operand_1), .Operand_2(Operand_2), .Result(AND_result), .Updated_Flags(AND_updated_flags),
    .Current_Flags(Current_Flags));
  OR OR (
    .Operand_1(Operand_1), .Operand_2(Operand_2), .Result(OR_result), .Updated_Flags(OR_updated_flags),
    .Current_Flags(Current_Flags));
  XOR XOR (
    .Operand_1(Operand_1), .Operand_2(Operand_2), .Result(XOR_result), .Updated_Flags(XOR_updated_flags),
    .Current_Flags(Current_Flags));
  Add ADD (
    .Current_Flags(Current_Flags), .Operand_1(Operand_1), .Operand_2(Operand_2),
    .Updated_Flags(ADD_updated_flags), .Result(ADD_result));
  Subtract SUB (
    .Current_Flags(Current_Flags), .Operand_1(Operand_1), .Operand_2(Operand_2),
    .Updated_Flags(SUB_updated_flags), .Result(SUB_result));
  Multiply MUL (
    .Current_Flags(Current_Flags), .Operand_1(Operand_1), .Operand_2(Operand_2),
    .Updated_Flags(MUL_updated_flags), .Result(MUL_result));
  Save_Flags SAVE_FLAGS (.Current_Flags(Current_Flags), .Flags_Saved_to_Rd(SAVE_FLAGS_flags_saved_to_rd));
  BitSelector #(.width(16), .group(4)) bitselector_1 (.in(Op_Code), .out(bitselector_1_out), .sel(2'b11));
  Multiplexer #(.select(4), .width(16)) multiplexer_1 (
    .in0(Operand_2), .in1(Operand_2), .in2(Operand_2), .in3(Operand_2), .in4(Operand_2), .in5(Operand_2),
    .in6(Operand_2), .in7(Operand_2), .in8(AND_result), .in9(OR_result), .in10(ADD_result),
    .in11(SUB_result), .in12(MUL_result), .in13(XOR_result), .in14(Operand_2), .in15(Operand_2),
    .out(multiplexer_1_out), .sel(bitselector_1_out));  // open: en
  Multiplexer #(.select(4), .width(5)) multiplexer_2 (
    .in0(Current_Flags), .in1(Current_Flags), .in2(Current_Flags), .in3(Current_Flags), .in4(Current_Flags),
    .in5(Current_Flags), .in6(Current_Flags), .in7(Current_Flags), .in8(AND_updated_flags),
    .in9(OR_updated_flags), .in10(ADD_updated_flags), .in11(SUB_updated_flags), .in12(MUL_updated_flags),
    .in13(XOR_updated_flags), .in14(Current_Flags), .in15(Current_Flags), .out(multiplexer_2_out),
    .sel(bitselector_1_out));  // open: en
  LSL LSL (
    .Current_Flags(Current_Flags), .Operand_1(multiplexer_1_out), .Updated_Flags(LSL_updated_flags),
    .Result(LSL_result));
  LSR LSR (
    .Updated_Flags(LSR_updated_flags), .Current_Flags(Current_Flags), .Operand_1(multiplexer_1_out),
    .Result(LSR_result));
  LSL8 LSL8 (
    .Current_Flags(Current_Flags), .Operand_1(multiplexer_1_out), .Updated_Flags(LSL8_updated_flags),
    .Result(LSL8_result));
  LSR8 LSR8 (
    .Updated_Flags(LSR8_updated_flags), .Current_Flags(Current_Flags), .Operand_1(multiplexer_1_out),
    .Result(LSR8_result));
  ASL ASL (
    .Current_Flags(Current_Flags), .Operand_1(multiplexer_1_out), .Updated_Flags(ASL_updated_flags),
    .Result(ASL_result));
  ASR ASR (
    .Current_Flags(Current_Flags), .Operand_1(multiplexer_1_out), .Updated_Flags(ASR_updated_flags),
    .Result(ASR_result));
  BitSelector #(.width(16), .group(4)) bitselector_2 (.in(Op_Code), .out(bitselector_2_out), .sel(2'b01));
  BitSelector #(.width(16)) bitselector_3 (.in(Op_Code), .out(bitselector_3_out), .sel(4'b1111));
  Multiplexer #(.select(4), .width(16)) multiplexer_3 (
    .in0(LSL_result), .in1(LSR_result), .in2(LSL8_result), .in3(LSR8_result), .in4(ASL_result),
    .in5(ASR_result), .in6(multiplexer_1_out), .in7(SAVE_FLAGS_flags_saved_to_rd), .in8(multiplexer_1_out),
    .in9(multiplexer_1_out), .in10(multiplexer_1_out), .in11(multiplexer_1_out), .in12(multiplexer_1_out),
    .in13(multiplexer_1_out), .in14(multiplexer_1_out), .in15(multiplexer_1_out),
    .out(Arith_Bit_Shift_Result), .sel(or_2_out));  // open: en
  assign bit_extender_1_out = {{3{bitselector_3_out}}, bitselector_3_out};  // Bit_Extender bit_extender_1
  Multiplexer #(.select(4), .width(5)) multiplexer_4 (
    .in0(LSL_updated_flags), .in1(LSR_updated_flags), .in2(LSL8_updated_flags), .in3(LSR8_updated_flags),
    .in4(ASL_updated_flags), .in5(ASR_updated_flags), .in6(multiplexer_2_out), .in7(multiplexer_2_out),
    .in8(multiplexer_2_out), .in9(multiplexer_2_out), .in10(multiplexer_2_out), .in11(multiplexer_2_out),
    .in12(multiplexer_2_out), .in13(multiplexer_2_out), .in14(multiplexer_2_out), .in15(multiplexer_2_out),
    .out(Arith_Bit_Shift_Updated_Flags), .sel(or_2_out));  // open: en
  assign or_2_out = bitselector_2_out | bit_extender_1_out;  // OR_Gate or_2, 4 bits wide
endmodule

module Set_Inc_Decr (
  input  [15:0] Operand_1,
  input  [15:0] Operand_2,
  input  [4:0] Current_Flags,
  input  [15:0] Op_Code,
  output [15:0] Set_Inc_Dec_Result,
  output [4:0] Set_Inc_Dec_Updated_Flags
);

  wire bitselector_3_out, bitselector_4_out, bitselector_5_out;
  wire [3:0] bitselector_1_out, bitselector_2_out;
  wire [4:0] DEC_updated_flags, INC_updated_flags, multiplexer_2_out;
  wire [15:0] DEC_result, INC_result, multiplexer_1_out, multiplexer_3_out, SETHI_result, SETLO_result;

  BitSelector #(.width(16), .group(4)) bitselector_1 (.in(Op_Code), .out(bitselector_1_out), .sel(2'b01));
  BitSelector #(.width(16), .group(4)) bitselector_2 (.in(Op_Code), .out(bitselector_2_out), .sel(2'b11));
  BitSelector #(.width(16)) bitselector_3 (.in(Op_Code), .out(bitselector_3_out), .sel(4'b1111));
  BitSelector #(.width(4)) bitselector_4 (.in(bitselector_1_out), .out(bitselector_4_out), .sel(2'b10));
  BitSelector #(.width(4)) bitselector_5 (.in(bitselector_2_out), .out(bitselector_5_out), .sel(2'b00));
  Increment INC (
    .Current_Flags(Current_Flags), .Op_Code(Op_Code), .Contents_of_Rd(Operand_1),
    .Updated_Flags(INC_updated_flags), .Result(INC_result));
  Decrement DEC (
    .Current_Flags(Current_Flags), .Op_Code(Op_Code), .Contents_of_Rd(Operand_1),
    .Updated_Flags(DEC_updated_flags), .Result(DEC_result));
  SetLO SETLO (.Op_Code(Op_Code), .Result(SETLO_result));
  SetHI SETHI (.Op_Code(Op_Code), .Contents_from_Rd(Operand_1), .Result(SETHI_result));
  Multiplexer #(.width(16)) multiplexer_1 (
    .in0(INC_result), .in1(DEC_result), .out(multiplexer_1_out), .sel(bitselector_4_out));  // open: en
  Multiplexer #(.width(5)) multiplexer_2 (
    .in0(INC_updated_flags), .in1(DEC_updated_flags), .out(multiplexer_2_out), .sel(bitselector_4_out));  // open: en
  Multiplexer #(.width(16)) multiplexer_3 (
    .in0(SETLO_result), .in1(SETHI_result), .out(multiplexer_3_out), .sel(bitselector_5_out));  // open: en
  Multiplexer #(.width(16)) multiplexer_4 (
    .in0(multiplexer_1_out), .in1(multiplexer_3_out), .out(Set_Inc_Dec_Result), .sel(bitselector_3_out));  // open: en
  Multiplexer #(.width(5)) multiplexer_5 (
    .in0(multiplexer_2_out), .in1(Current_Flags), .out(Set_Inc_Dec_Updated_Flags), .sel(bitselector_3_out));  // open: en

  // Notes on the sheet:
  //   bits 4-7
  //   bits 12-15
  //   bit 6
  //   bit 12
  //   Set Result
  //   Inc/Dec Result
  //   Inc/Dec Flags
  //   set doesn't change flags
endmodule

module SetLO (
  input  [15:0] Op_Code,
  output [15:0] Result
);

  wire [7:0] bitselector_1_out;

  BitSelector #(.width(16), .group(8)) bitselector_1 (.in(Op_Code), .out(bitselector_1_out), .sel(1'b0));
  assign Result = {{8{bitselector_1_out[7]}}, bitselector_1_out};  // Bit_Extender bit_extender_1
endmodule

module SetHI (
  input  [15:0] Op_Code,
  input  [15:0] Contents_from_Rd,
  output [15:0] Result
);

  BitSelector #(.width(16), .group(8)) bitselector_1 (.in(Op_Code), .out(Result[15:8]), .sel(1'b0));
  BitSelector #(.width(16), .group(8)) bitselector_2 (.in(Contents_from_Rd), .out(Result[7:0]), .sel(1'b0));
endmodule

module AND (
  input  [4:0] Current_Flags,
  input  [15:0] Operand_1,
  input  [15:0] Operand_2,
  output [4:0] Updated_Flags,
  output [15:0] Result
);

  assign Result = Operand_1 & Operand_2;  // AND_Gate and_1, 16 bits wide
  Comparator #(.width(16)) comparator_1 (.a(Result), .b({16{1'b0}}), .eq(Updated_Flags[1]));  // open: gt, lt
  BitSelector #(.width(16)) bitselector_1 (.in(Result), .out(Updated_Flags[0]), .sel(4'b1111));

  assign Updated_Flags[4:2] = Current_Flags[4:2];

  // Notes on the sheet:
  //   z
  //   s
endmodule

module OR (
  input  [4:0] Current_Flags,
  input  [15:0] Operand_1,
  input  [15:0] Operand_2,
  output [4:0] Updated_Flags,
  output [15:0] Result
);

  assign Result = Operand_1 | Operand_2;  // OR_Gate or_1, 16 bits wide
  Comparator #(.width(16)) comparator_1 (.a(Result), .b({16{1'b0}}), .eq(Updated_Flags[1]));  // open: gt, lt
  BitSelector #(.width(16)) bitselector_1 (.in(Result), .out(Updated_Flags[0]), .sel(4'b1111));

  assign Updated_Flags[4:2] = Current_Flags[4:2];

  // Notes on the sheet:
  //   z
  //   s
endmodule

module XOR (
  input  [4:0] Current_Flags,
  input  [15:0] Operand_1,
  input  [15:0] Operand_2,
  output [4:0] Updated_Flags,
  output [15:0] Result
);

  assign Result = Operand_1 ^ Operand_2;  // XOR_Gate xor_1, 16 bits wide
  Comparator #(.width(16)) comparator_1 (.a(Result), .b({16{1'b0}}), .eq(Updated_Flags[1]));  // open: gt, lt
  BitSelector #(.width(16)) bitselector_1 (.in(Result), .out(Updated_Flags[0]), .sel(4'b1111));

  assign Updated_Flags[4:2] = Current_Flags[4:2];

  // Notes on the sheet:
  //   z
  //   s
endmodule

module Add (
  input  [4:0] Current_Flags,
  input  [15:0] Operand_1,
  input  [15:0] Operand_2,
  output [4:0] Updated_Flags,
  output [15:0] Result
);

  wire and_1_out, and_2_out, and_3_out, bitselector_1_out, bitselector_2_out, bitselector_3_out, nor_1_out,
       not_1_out, not_2_out;

  not not_1 (not_1_out, Current_Flags[4]);
  and and_1 (and_1_out, not_1_out, Current_Flags[3]);
  Adder #(.width(16)) adder_1 (.a(Operand_1), .b(Operand_2), .out(Result), .cin(and_1_out), .cout(Updated_Flags[3]));
  BitSelector #(.width(16)) bitselector_1 (.in(Operand_1), .out(bitselector_1_out), .sel(4'b1111));
  BitSelector #(.width(16)) bitselector_2 (.in(Operand_2), .out(bitselector_2_out), .sel(4'b1111));
  BitSelector #(.width(16)) bitselector_3 (.in(Result), .out(bitselector_3_out), .sel(4'b1111));
  and and_2 (and_2_out, bitselector_1_out, bitselector_2_out, not_2_out);
  nor nor_1 (nor_1_out, bitselector_2_out, bitselector_1_out);
  not not_2 (not_2_out, bitselector_3_out);
  BitSelector #(.width(16)) bitselector_4 (.in(Result), .out(Updated_Flags[0]), .sel(4'b1111));
  Comparator #(.width(16)) comparator_1 (.a(Result), .b({16{1'b0}}), .eq(Updated_Flags[1]));  // open: gt, lt
  and and_3 (and_3_out, nor_1_out, bitselector_3_out);
  or or_1 (Updated_Flags[2], and_2_out, and_3_out);

  assign Updated_Flags[4] = Current_Flags[4];

  // Notes on the sheet:
  //   carry block
  //   carry
  //   Overflow Detection
  //   (if input signs match, and output sign is flipped)
  //   s
  //   z
  //   v
endmodule

module Subtract (
  input  [4:0] Current_Flags,
  input  [15:0] Operand_1,
  input  [15:0] Operand_2,
  output [4:0] Updated_Flags,
  output [15:0] Result
);

  wire and_1_out, and_2_out, and_3_out, bitselector_1_out, bitselector_2_out, bitselector_3_out, not_1_out,
       not_2_out, not_4_out, not_5_out, not_6_out, subtractor_1_bout;

  not not_1 (not_1_out, Current_Flags[4]);
  and and_1 (and_1_out, not_1_out, not_2_out);
  not not_2 (not_2_out, Current_Flags[3]);
  Subtractor #(.width(16)) subtractor_1 (
    .a(Operand_1), .b(Operand_2), .out(Result), .bin(and_1_out), .bout(subtractor_1_bout));
  not not_3 (Updated_Flags[3], subtractor_1_bout);
  BitSelector #(.width(16)) bitselector_1 (.in(Result), .out(bitselector_1_out), .sel(4'b1111));
  BitSelector #(.width(16)) bitselector_2 (.in(Operand_1), .out(bitselector_2_out), .sel(4'b1111));
  BitSelector #(.width(16)) bitselector_3 (.in(Operand_2), .out(bitselector_3_out), .sel(4'b1111));
  not not_4 (not_4_out, bitselector_1_out);
  not not_5 (not_5_out, bitselector_3_out);
  not not_6 (not_6_out, bitselector_2_out);
  BitSelector #(.width(16)) bitselector_4 (.in(Result), .out(Updated_Flags[0]), .sel(4'b1111));
  Comparator #(.width(16)) comparator_1 (.a(Result), .b({16{1'b0}}), .eq(Updated_Flags[1]));  // open: gt, lt
  and and_2 (and_2_out, not_4_out, bitselector_2_out, not_5_out);
  and and_3 (and_3_out, bitselector_1_out, bitselector_3_out, not_6_out);
  or or_1 (Updated_Flags[2], and_2_out, and_3_out);

  assign Updated_Flags[4] = Current_Flags[4];

  // Notes on the sheet:
  //   carry block
  //   carry
  //   Overflow Detection
  //   (Both inputs have diff signs, result has same sign as the subtracting input)
  //   s
  //   z
  //   c
  //   v
endmodule

module Multiply (
  input  [4:0] Current_Flags,
  input  [15:0] Operand_1,
  input  [15:0] Operand_2,
  output [4:0] Updated_Flags,
  output [15:0] Result
);

  wire and_1_out, comparator_1_lt, comparator_3_eq, comparator_4_eq, not_1_out, not_2_out, not_3_out,
       not_4_out, or_1_out;
  wire [15:0] bitselector_1_out, bitselector_2_out, bitselector_3_out;
  wire [31:0] bit_extender_1_out, bit_extender_2_out, bit_extender_3_out, bit_extender_4_out,
       multiplier_1_out, multiplier_2_out;

  not not_1 (not_1_out, Current_Flags[1]);
  not not_2 (not_2_out, Current_Flags[2]);
  not not_3 (not_3_out, Current_Flags[3]);
  not not_4 (not_4_out, Current_Flags[4]);
  assign bit_extender_1_out = {{16{1'b0}}, Operand_1};  // Bit_Extender bit_extender_1
  assign bit_extender_2_out = {{16{1'b0}}, Operand_2};  // Bit_Extender bit_extender_2
  assign bit_extender_3_out = {{16{Operand_1[15]}}, Operand_1};  // Bit_Extender bit_extender_3
  assign bit_extender_4_out = {{16{Operand_2[15]}}, Operand_2};  // Bit_Extender bit_extender_4
  and and_1 (and_1_out, Current_Flags[0], not_1_out, not_2_out, not_3_out, not_4_out);
  Multiplier #(.width(32)) multiplier_1 (
    .a(bit_extender_1_out), .b(bit_extender_2_out), .out(multiplier_1_out));  // open: cin, cout
  Multiplier #(.width(32)) multiplier_2 (
    .a(bit_extender_3_out), .b(bit_extender_4_out), .out(multiplier_2_out));  // open: cin, cout
  BitSelector #(.width(32), .group(16)) bitselector_1 (.in(multiplier_1_out), .out(bitselector_1_out), .sel(1'b0));
  Multiplexer #(.width(16)) multiplexer_1 (
    .in0(bitselector_1_out), .in1(bitselector_2_out), .out(Result), .sel(and_1_out));  // open: en
  BitSelector #(.width(32), .group(16)) bitselector_2 (.in(multiplier_2_out), .out(bitselector_2_out), .sel(1'b1));
  BitSelector #(.width(32), .group(16)) bitselector_3 (.in(multiplier_2_out), .out(bitselector_3_out), .sel(1'b1));
  BitSelector #(.width(32)) bitselector_4 (.in(multiplier_1_out), .out(Updated_Flags[0]), .sel(5'b01111));
  Comparator #(.width(32)) comparator_1 (.a(multiplier_1_out), .b(32'h10000), .lt(comparator_1_lt));  // open: gt, eq
  not not_5 (Updated_Flags[3], comparator_1_lt);
  Comparator #(.width(16)) comparator_2 (.a(Result), .b({16{1'b0}}), .eq(Updated_Flags[1]));  // open: gt, lt
  Comparator #(.width(16)) comparator_3 (.a(bitselector_3_out), .b({16{1'b0}}), .eq(comparator_3_eq));  // open: gt, lt
  or or_1 (or_1_out, comparator_3_eq, comparator_4_eq);
  Comparator #(.width(16)) comparator_4 (.a(bitselector_3_out), .b({16{1'b1}}), .eq(comparator_4_eq));  // open: gt, lt
  not not_6 (Updated_Flags[2], or_1_out);

  assign Updated_Flags[4] = Current_Flags[4];

  // Notes on the sheet:
  //   Unsigned MUL
  //   Signed MUL
  //   only s is true
  //   (and all other undefined cases)
  //   low 16 bits
  //   high 16 bits
  //   only s is true
  //   s
  //   c
  //   z
  //   v
endmodule

module Increment (
  input  [4:0] Current_Flags,
  input  [15:0] Contents_of_Rd,
  input  [15:0] Op_Code,
  output [4:0] Updated_Flags,
  output [15:0] Result
);

  wire and_1_out, and_2_out, bitselector_2_out, bitselector_3_out, bitselector_4_out, nor_1_out, not_1_out;
  wire [5:0] bitselector_1_out;
  wire [15:0] adder_1_out, bit_extender_1_out;

  BitSelector #(.width(16), .group(6)) bitselector_1 (.in(Op_Code), .out(bitselector_1_out), .sel(2'b00));
  assign bit_extender_1_out = {{10{1'b0}}, bitselector_1_out};  // Bit_Extender bit_extender_1
  Adder #(.width(16)) adder_1 (.a(bit_extender_1_out), .b(16'h1), .out(adder_1_out));  // open: cin, cout
  Adder #(.width(16)) adder_2 (
    .a(Contents_of_Rd), .b(adder_1_out), .out(Result), .cout(Updated_Flags[3]));  // open: cin
  BitSelector #(.width(16)) bitselector_2 (.in(Contents_of_Rd), .out(bitselector_2_out), .sel(4'b1111));
  BitSelector #(.width(16)) bitselector_3 (.in(adder_1_out), .out(bitselector_3_out), .sel(4'b1111));
  BitSelector #(.width(16)) bitselector_4 (.in(Result), .out(bitselector_4_out), .sel(4'b1111));
  and and_1 (and_1_out, bitselector_2_out, bitselector_3_out, not_1_out);
  not not_1 (not_1_out, bitselector_4_out);
  Comparator #(.width(16)) comparator_1 (.a(Result), .b({16{1'b0}}), .eq(Updated_Flags[1]));  // open: gt, lt
  BitSelector #(.width(16)) bitselector_5 (.in(Result), .out(Updated_Flags[0]), .sel(4'b1111));
  nor nor_1 (nor_1_out, bitselector_3_out, bitselector_2_out);
  and and_2 (and_2_out, nor_1_out, bitselector_4_out);
  or or_1 (Updated_Flags[2], and_1_out, and_2_out);

  assign Updated_Flags[4] = Current_Flags[4];

  // Notes on the sheet:
  //   Inc by last 6 bits + 1; pad rest
  //   z
  //   s
  //   v
endmodule

module Decrement (
  input  [4:0] Current_Flags,
  input  [15:0] Contents_of_Rd,
  input  [15:0] Op_Code,
  output [4:0] Updated_Flags,
  output [15:0] Result
);

  wire and_1_out, and_2_out, bitselector_2_out, bitselector_3_out, bitselector_4_out, not_1_out, not_2_out,
       not_3_out, subtractor_1_bout;
  wire [5:0] bitselector_1_out;
  wire [15:0] adder_1_out, bit_extender_1_out;

  BitSelector #(.width(16), .group(6)) bitselector_1 (.in(Op_Code), .out(bitselector_1_out), .sel(2'b00));
  assign bit_extender_1_out = {{10{1'b0}}, bitselector_1_out};  // Bit_Extender bit_extender_1
  Adder #(.width(16)) adder_1 (.a(bit_extender_1_out), .b(16'h1), .out(adder_1_out));  // open: cin, cout
  Subtractor #(.width(16)) subtractor_1 (
    .a(Contents_of_Rd), .b(adder_1_out), .out(Result), .bout(subtractor_1_bout));  // open: bin
  BitSelector #(.width(16)) bitselector_2 (.in(Result), .out(bitselector_2_out), .sel(4'b1111));
  BitSelector #(.width(16)) bitselector_3 (.in(Contents_of_Rd), .out(bitselector_3_out), .sel(4'b1111));
  BitSelector #(.width(16)) bitselector_4 (.in(adder_1_out), .out(bitselector_4_out), .sel(4'b1111));
  not not_1 (not_1_out, bitselector_2_out);
  and and_1 (and_1_out, not_1_out, bitselector_3_out, not_2_out);
  not not_2 (not_2_out, bitselector_4_out);
  and and_2 (and_2_out, bitselector_2_out, bitselector_4_out, not_3_out);
  not not_3 (not_3_out, bitselector_3_out);
  not not_4 (Updated_Flags[3], subtractor_1_bout);
  Comparator #(.width(16)) comparator_1 (.a(Result), .b({16{1'b0}}), .eq(Updated_Flags[1]));  // open: gt, lt
  BitSelector #(.width(16)) bitselector_5 (.in(Result), .out(Updated_Flags[0]), .sel(4'b1111));
  or or_1 (Updated_Flags[2], and_1_out, and_2_out);

  assign Updated_Flags[4] = Current_Flags[4];

  // Notes on the sheet:
  //   Dec by last 6 bits + 1; pad rest
  //   Overflow Detection
  //   (Both inputs have diff signs, result has same sign as the subtracting input)
  //   c
  //   z
  //   s
  //   v
endmodule

module LSL (
  input  [4:0] Current_Flags,
  input  [15:0] Operand_1,
  output [4:0] Updated_Flags,
  output [15:0] Result
);

  wire and_1_out, not_1_out;
  wire [15:0] adder_1_out, shifter_1_out;

  not not_1 (not_1_out, Current_Flags[4]);
  Shifter #(.width(16)) shifter_1 (.in(Operand_1), .\dist (4'b0001), .out(shifter_1_out));
  and and_1 (and_1_out, not_1_out, Current_Flags[3]);
  Adder #(.width(16)) adder_1 (.a(shifter_1_out), .b(16'h1), .out(adder_1_out));  // open: cin, cout
  Multiplexer #(.width(16)) multiplexer_1 (
    .in0(shifter_1_out), .in1(adder_1_out), .out(Result), .sel(and_1_out));  // open: en
  Comparator #(.width(16)) comparator_1 (.a(Result), .b({16{1'b0}}), .eq(Updated_Flags[1]));  // open: gt, lt
  BitSelector #(.width(16)) bitselector_1 (.in(Result), .out(Updated_Flags[0]), .sel(4'b1111));
  BitSelector #(.width(16)) bitselector_2 (.in(Operand_1), .out(Updated_Flags[3]), .sel(4'b1111));

  assign {Updated_Flags[4], Updated_Flags[2]} = {Current_Flags[4], Current_Flags[2]};

  // Notes on the sheet:
  //   carry block
  //   carry
  //   z
  //   s
  //   c
endmodule

module LSR (
  input  [4:0] Current_Flags,
  input  [15:0] Operand_1,
  output [4:0] Updated_Flags,
  output [15:0] Result
);

  wire and_1_out, not_1_out;
  wire [15:0] adder_1_out, shifter_1_out;

  not not_1 (not_1_out, Current_Flags[4]);
  Shifter #(.width(16), .shift("lr")) shifter_1 (.in(Operand_1), .\dist (4'b0001), .out(shifter_1_out));
  and and_1 (and_1_out, not_1_out, Current_Flags[3]);
  Adder #(.width(16)) adder_1 (.a(shifter_1_out), .b(16'h8000), .out(adder_1_out));  // open: cin, cout
  Multiplexer #(.width(16)) multiplexer_1 (
    .in0(shifter_1_out), .in1(adder_1_out), .out(Result), .sel(and_1_out));  // open: en
  Comparator #(.width(16)) comparator_1 (.a(Result), .b({16{1'b0}}), .eq(Updated_Flags[1]));  // open: gt, lt
  BitSelector #(.width(16)) bitselector_1 (.in(Result), .out(Updated_Flags[0]), .sel(4'b1111));
  BitSelector #(.width(16)) bitselector_2 (.in(Operand_1), .out(Updated_Flags[3]), .sel(4'b0000));

  assign {Updated_Flags[4], Updated_Flags[2]} = {Current_Flags[4], Current_Flags[2]};

  // Notes on the sheet:
  //   carry block
  //   carry
  //   z
  //   s
  //   c
endmodule

module LSL8 (
  input  [4:0] Current_Flags,
  input  [15:0] Operand_1,
  output [4:0] Updated_Flags,
  output [15:0] Result
);

  Shifter #(.width(16)) shifter_1 (.in(Operand_1), .\dist (4'b1000), .out(Result));
  Comparator #(.width(16)) comparator_1 (.a(Result), .b({16{1'b0}}), .eq(Updated_Flags[1]));  // open: gt, lt
  BitSelector #(.width(16)) bitselector_1 (.in(Result), .out(Updated_Flags[0]), .sel(4'b1111));

  assign Updated_Flags[4:2] = Current_Flags[4:2];

  // Notes on the sheet:
  //   z
  //   s
endmodule

module LSR8 (
  input  [4:0] Current_Flags,
  input  [15:0] Operand_1,
  output [4:0] Updated_Flags,
  output [15:0] Result
);

  Shifter #(.width(16), .shift("lr")) shifter_1 (.in(Operand_1), .\dist (4'b1000), .out(Result));
  Comparator #(.width(16)) comparator_1 (.a(Result), .b({16{1'b0}}), .eq(Updated_Flags[1]));  // open: gt, lt
  BitSelector #(.width(16)) bitselector_1 (.in(Result), .out(Updated_Flags[0]), .sel(4'b1111));

  assign Updated_Flags[4:2] = Current_Flags[4:2];

  // Notes on the sheet:
  //   z
  //   s
endmodule

module ASL (
  input  [4:0] Current_Flags,
  input  [15:0] Operand_1,
  output [4:0] Updated_Flags,
  output [15:0] Result
);

  wire and_1_out, and_2_out, and_3_out, bitselector_1_out, bitselector_2_out, nor_1_out, not_1_out, not_2_out;
  wire [15:0] adder_1_out, adder_2_out, shifter_1_out;

  not not_1 (not_1_out, Current_Flags[4]);
  Shifter #(.width(16)) shifter_1 (.in(Operand_1), .\dist (4'b0001), .out(shifter_1_out));
  BitSelector #(.width(16)) bitselector_1 (.in(Operand_1), .out(bitselector_1_out), .sel(4'b1111));
  Adder #(.width(16)) adder_1 (.a(Operand_1), .b(Operand_1), .out(adder_1_out));  // open: cin, cout
  and and_1 (and_1_out, not_1_out, Current_Flags[3]);
  Adder #(.width(16)) adder_2 (.a(shifter_1_out), .b(16'h1), .out(adder_2_out));  // open: cin, cout
  BitSelector #(.width(16)) bitselector_2 (.in(adder_1_out), .out(bitselector_2_out), .sel(4'b1111));
  Multiplexer #(.width(16)) multiplexer_1 (
    .in0(shifter_1_out), .in1(adder_2_out), .out(Result), .sel(and_1_out));  // open: en
  nor nor_1 (nor_1_out, bitselector_1_out, bitselector_1_out);
  not not_2 (not_2_out, bitselector_2_out);
  and and_2 (and_2_out, bitselector_1_out, bitselector_1_out, not_2_out);
  and and_3 (and_3_out, nor_1_out, bitselector_2_out);
  BitSelector #(.width(16)) bitselector_3 (.in(Result), .out(Updated_Flags[0]), .sel(4'b1111));
  BitSelector #(.width(16)) bitselector_4 (.in(Operand_1), .out(Updated_Flags[3]), .sel(4'b1111));
  Comparator #(.width(16)) comparator_1 (.a(Result), .b({16{1'b0}}), .eq(Updated_Flags[1]));  // open: gt, lt
  or or_1 (Updated_Flags[2], and_2_out, and_3_out);

  assign Updated_Flags[4] = Current_Flags[4];

  // Notes on the sheet:
  //   carry
  //   carry block
  //   Overflow
  //   (v receives value it would have after ADD)
  //   z
  //   s
  //   c
  //   v
endmodule

module ASR (
  input  [4:0] Current_Flags,
  input  [15:0] Operand_1,
  output [4:0] Updated_Flags,
  output [15:0] Result
);

  Shifter #(.width(16), .shift("ar")) shifter_1 (.in(Operand_1), .\dist (4'b0001), .out(Result));
  Comparator #(.width(16)) comparator_1 (.a(Result), .b({16{1'b0}}), .eq(Updated_Flags[1]));  // open: gt, lt
  BitSelector #(.width(16)) bitselector_1 (.in(Result), .out(Updated_Flags[0]), .sel(4'b1111));
  BitSelector #(.width(16)) bitselector_2 (.in(Operand_1), .out(Updated_Flags[3]), .sel(4'b0000));

  assign {Updated_Flags[4], Updated_Flags[2]} = {Current_Flags[4], Current_Flags[2]};

  // Notes on the sheet:
  //   z
  //   s
  //   c
endmodule

module Setting_Restoring_Flags (
  input  [15:0] Op_Code,
  input  [4:0] Current_Flags,
  input  [15:0] Contents_of_Rd,
  output [4:0] Updated_Flags__Set_Restore
);

  wire comparator_1_eq;
  wire [2:0] bitselector_1_out;
  wire [3:0] bitselector_2_out;
  wire [4:0] FOFF_updated_flags__set, FON_updated_flags__set, FSET4_updated_flags__set,
       FSET5_updated_flags__set, multiplexer_1_out, RESTORE_FLAGS_restored_flags;

  Restore_Flags RESTORE_FLAGS (.Contents_of_Rd(Contents_of_Rd), .Restored_Flags(RESTORE_FLAGS_restored_flags));
  BitSelector #(.width(16), .group(3)) bitselector_1 (.in(Op_Code), .out(bitselector_1_out), .sel(3'b011));
  BitSelector #(.width(16), .group(4)) bitselector_2 (.in(Op_Code), .out(bitselector_2_out), .sel(2'b01));
  FON FON (.Op_Code(Op_Code), .Current_Flags(Current_Flags), .Updated_Flags__Set(FON_updated_flags__set));
  FOFF FOFF (.Op_Code(Op_Code), .Current_Flags(Current_Flags), .Updated_Flags__Set(FOFF_updated_flags__set));
  FSET5 FSET5 (.Op_Code(Op_Code), .Updated_Flags__Set(FSET5_updated_flags__set));
  FSET4 FSET4 (.Op_Code(Op_Code), .Current_Flags(Current_Flags), .Updated_Flags__Set(FSET4_updated_flags__set));
  Comparator #(.width(4)) comparator_1 (.a(bitselector_2_out), .b(4'b0111), .eq(comparator_1_eq));  // open: gt, lt
  Multiplexer #(.select(3), .width(5)) multiplexer_1 (
    .in0(FON_updated_flags__set), .in2(FSET5_updated_flags__set), .in4(FOFF_updated_flags__set),
    .in6(FSET4_updated_flags__set), .out(multiplexer_1_out), .sel(bitselector_1_out));  // open: in1, in3, in5, in7, en
  Multiplexer #(.width(5)) multiplexer_2 (
    .in0(multiplexer_1_out), .in1(RESTORE_FLAGS_restored_flags), .out(Updated_Flags__Set_Restore),
    .sel(comparator_1_eq));  // open: en

  // Notes on the sheet:
  //   Flag Op (bits 9-11)
  //   Restoring (bits 4-7)
endmodule

module Save_Flags (
  input  [4:0] Current_Flags,
  output [15:0] Flags_Saved_to_Rd
);

  assign Flags_Saved_to_Rd = {{11{1'b0}}, Current_Flags};  // Bit_Extender bit_extender_1
endmodule

module Restore_Flags (
  input  [15:0] Contents_of_Rd,
  output [4:0] Restored_Flags
);

  BitSelector #(.width(16), .group(5)) bitselector_1 (.in(Contents_of_Rd), .out(Restored_Flags), .sel(2'b00));
endmodule

module FON (
  input  [15:0] Op_Code,
  input  [4:0] Current_Flags,
  output [4:0] Updated_Flags__Set
);

  wire bitselector_1_out;
  wire [3:0] bitselector_2_out;
  wire [4:0] adder_1_out, bit_extender_1_out, bit_extender_2_out, shifter_1_out;

  BitSelector #(.width(16)) bitselector_1 (.in(Op_Code), .out(bitselector_1_out), .sel(4'b1000));
  BitSelector #(.width(16), .group(4)) bitselector_2 (.in(Op_Code), .out(bitselector_2_out), .sel(2'b00));
  assign bit_extender_1_out = {{4{1'b0}}, bitselector_1_out};  // Bit_Extender bit_extender_1
  assign bit_extender_2_out = {{1{1'b0}}, bitselector_2_out};  // Bit_Extender bit_extender_2
  Shifter #(.width(5)) shifter_1 (.in(bit_extender_1_out), .\dist (3'b100), .out(shifter_1_out));
  Adder #(.width(5)) adder_1 (.a(shifter_1_out), .b(bit_extender_2_out), .out(adder_1_out));  // open: cin, cout
  assign Updated_Flags__Set = adder_1_out | Current_Flags;  // OR_Gate or_1, 5 bits wide

  // Notes on the sheet:
  //   v4
  //   v3 v2 v1 v0
  //   v4 v3 v2 v1 v1 v0
endmodule

module FOFF (
  input  [15:0] Op_Code,
  input  [4:0] Current_Flags,
  output [4:0] Updated_Flags__Set
);

  wire bitselector_1_out;
  wire [3:0] bitselector_2_out;
  wire [4:0] adder_1_out, bit_extender_1_out, bit_extender_2_out, not_1_out, shifter_1_out;

  BitSelector #(.width(16)) bitselector_1 (.in(Op_Code), .out(bitselector_1_out), .sel(4'b1000));
  BitSelector #(.width(16), .group(4)) bitselector_2 (.in(Op_Code), .out(bitselector_2_out), .sel(2'b00));
  assign bit_extender_1_out = {{4{1'b0}}, bitselector_1_out};  // Bit_Extender bit_extender_1
  assign bit_extender_2_out = {{1{1'b0}}, bitselector_2_out};  // Bit_Extender bit_extender_2
  Shifter #(.width(5)) shifter_1 (.in(bit_extender_1_out), .\dist (3'b100), .out(shifter_1_out));
  Adder #(.width(5)) adder_1 (.a(shifter_1_out), .b(bit_extender_2_out), .out(adder_1_out));  // open: cin, cout
  assign not_1_out = ~adder_1_out;  // NOT_Gate not_1, 5 bits wide
  assign Updated_Flags__Set = not_1_out & Current_Flags;  // AND_Gate and_1, 5 bits wide

  // Notes on the sheet:
  //   v4
  //   v3 v2 v1 v0
  //   v4 v3 v2 v1 v1 v0
endmodule

module FSET5 (
  input  [15:0] Op_Code,
  output [4:0] Updated_Flags__Set
);

  wire bitselector_1_out;
  wire [3:0] bitselector_2_out;
  wire [4:0] bit_extender_1_out, bit_extender_2_out, shifter_1_out;

  BitSelector #(.width(16)) bitselector_1 (.in(Op_Code), .out(bitselector_1_out), .sel(4'b1000));
  BitSelector #(.width(16), .group(4)) bitselector_2 (.in(Op_Code), .out(bitselector_2_out), .sel(2'b00));
  assign bit_extender_1_out = {{4{1'b0}}, bitselector_1_out};  // Bit_Extender bit_extender_1
  assign bit_extender_2_out = {{1{1'b0}}, bitselector_2_out};  // Bit_Extender bit_extender_2
  Shifter #(.width(5)) shifter_1 (.in(bit_extender_1_out), .\dist (3'b100), .out(shifter_1_out));
  Adder #(.width(5)) adder_1 (.a(shifter_1_out), .b(bit_extender_2_out), .out(Updated_Flags__Set));  // open: cin, cout

  // Notes on the sheet:
  //   v4
  //   v3 v2 v1 v0
  //   v4 v3 v2 v1 v1 v0
endmodule

module FSET4 (
  input  [15:0] Op_Code,
  input  [4:0] Current_Flags,
  output [4:0] Updated_Flags__Set
);

  wire bitselector_2_out;
  wire [3:0] bitselector_1_out;
  wire [4:0] bit_extender_1_out, bit_extender_2_out, shifter_1_out;

  BitSelector #(.width(16), .group(4)) bitselector_1 (.in(Op_Code), .out(bitselector_1_out), .sel(2'b00));
  BitSelector #(.width(5)) bitselector_2 (.in(Current_Flags), .out(bitselector_2_out), .sel(3'b100));
  assign bit_extender_1_out = {{1{1'b0}}, bitselector_1_out};  // Bit_Extender bit_extender_1
  assign bit_extender_2_out = {{4{1'b0}}, bitselector_2_out};  // Bit_Extender bit_extender_2
  Shifter #(.width(5)) shifter_1 (.in(bit_extender_2_out), .\dist (3'b100), .out(shifter_1_out));
  Adder #(.width(5)) adder_1 (.a(bit_extender_1_out), .b(shifter_1_out), .out(Updated_Flags__Set));  // open: cin, cout

  // Notes on the sheet:
  //   v3 v2 v1 v0
  //   v4
endmodule

module BR_BRR__Unconditional_Branch (
  input  [15:0] Op_Code,
  input  [15:0] Contents_of_Rb,
  input  [15:0] Current_Value_of_PC,
  output [15:0] New_Value_of_PC
);

  wire bitselector_2_out, not_1_out;
  wire [7:0] bitselector_1_out;
  wire [15:0] adder_1_out, bit_extender_1_out;

  BitSelector #(.width(16), .group(8)) bitselector_1 (.in(Op_Code), .out(bitselector_1_out), .sel(1'b0));
  BitSelector #(.width(16)) bitselector_2 (.in(Op_Code), .out(bitselector_2_out), .sel(4'b1100));
  assign bit_extender_1_out = {{8{bitselector_1_out[7]}}, bitselector_1_out};  // Bit_Extender bit_extender_1
  Adder #(.width(16)) adder_1 (.a(bit_extender_1_out), .b(Current_Value_of_PC), .out(adder_1_out));  // open: cin, cout
  not not_1 (not_1_out, bitselector_2_out);
  Multiplexer #(.width(16)) multiplexer_1 (
    .in0(Contents_of_Rb), .in1(adder_1_out), .out(New_Value_of_PC), .sel(not_1_out));  // open: en

  // Notes on the sheet:
  //   o (bits 0-7)
  //   bit 12
  //   BR
  //   BRR
endmodule

module BL_BLR (
  input  [15:0] Op_Code,
  input  [15:0] Contents_of_Rb,
  input  [15:0] Current_Value_of_PC,
  input  [4:0] Current_Flags,
  output [15:0] New_Value_of_PC
);

  wire bitselector_1_out, bitselector_2_out, bitselector_4_out, not_1_out, xor_1_out;
  wire [7:0] bitselector_3_out;
  wire [15:0] adder_1_out, adder_2_out, bit_extender_1_out, multiplexer_1_out;

  BitSelector #(.width(5)) bitselector_1 (.in(Current_Flags), .out(bitselector_1_out), .sel(3'b000));
  BitSelector #(.width(5)) bitselector_2 (.in(Current_Flags), .out(bitselector_2_out), .sel(3'b010));
  BitSelector #(.width(16), .group(8)) bitselector_3 (.in(Op_Code), .out(bitselector_3_out), .sel(1'b0));
  BitSelector #(.width(16)) bitselector_4 (.in(Op_Code), .out(bitselector_4_out), .sel(4'b1100));
  assign bit_extender_1_out = {{8{bitselector_3_out[7]}}, bitselector_3_out};  // Bit_Extender bit_extender_1
  Adder #(.width(16)) adder_1 (.a(bit_extender_1_out), .b(Current_Value_of_PC), .out(adder_1_out));  // open: cin, cout
  not not_1 (not_1_out, bitselector_4_out);
  xor xor_1 (xor_1_out, bitselector_1_out, bitselector_2_out);
  Multiplexer #(.width(16)) multiplexer_1 (
    .in0(Contents_of_Rb), .in1(adder_1_out), .out(multiplexer_1_out), .sel(not_1_out));  // open: en
  Adder #(.width(16)) adder_2 (.a(Current_Value_of_PC), .b(16'h1), .out(adder_2_out));  // open: cin, cout
  Multiplexer #(.width(16)) multiplexer_2 (
    .in0(adder_2_out), .in1(multiplexer_1_out), .out(New_Value_of_PC), .sel(xor_1_out));  // open: en

  // Notes on the sheet:
  //   o (bits 0-7)
  //   v
  //   bit 12
  //   s
  //   BL
  //   BLR
endmodule

module BGE_BGER (
  input  [15:0] Op_Code,
  input  [15:0] Contents_of_Rb,
  input  [15:0] Current_Value_of_PC,
  input  [4:0] Current_Flags,
  output [15:0] New_Value_of_PC
);

  wire bitselector_1_out, bitselector_2_out, bitselector_4_out, not_1_out, not_2_out, xor_1_out;
  wire [7:0] bitselector_3_out;
  wire [15:0] adder_1_out, adder_2_out, bit_extender_1_out, multiplexer_1_out;

  BitSelector #(.width(5)) bitselector_1 (.in(Current_Flags), .out(bitselector_1_out), .sel(3'b000));
  BitSelector #(.width(5)) bitselector_2 (.in(Current_Flags), .out(bitselector_2_out), .sel(3'b010));
  BitSelector #(.width(16), .group(8)) bitselector_3 (.in(Op_Code), .out(bitselector_3_out), .sel(1'b0));
  BitSelector #(.width(16)) bitselector_4 (.in(Op_Code), .out(bitselector_4_out), .sel(4'b1100));
  assign bit_extender_1_out = {{8{bitselector_3_out[7]}}, bitselector_3_out};  // Bit_Extender bit_extender_1
  Adder #(.width(16)) adder_1 (.a(bit_extender_1_out), .b(Current_Value_of_PC), .out(adder_1_out));  // open: cin, cout
  not not_1 (not_1_out, bitselector_4_out);
  xor xor_1 (xor_1_out, bitselector_1_out, bitselector_2_out);
  not not_2 (not_2_out, xor_1_out);
  Multiplexer #(.width(16)) multiplexer_1 (
    .in0(Contents_of_Rb), .in1(adder_1_out), .out(multiplexer_1_out), .sel(not_1_out));  // open: en
  Adder #(.width(16)) adder_2 (.a(Current_Value_of_PC), .b(16'h1), .out(adder_2_out));  // open: cin, cout
  Multiplexer #(.width(16)) multiplexer_2 (
    .in0(adder_2_out), .in1(multiplexer_1_out), .out(New_Value_of_PC), .sel(not_2_out));  // open: en

  // Notes on the sheet:
  //   o (bits 0-7)
  //   v
  //   bit 12
  //   s
  //   BGE
  //   BGER
endmodule
module BLE_BLER (
  input  [15:0] Op_Code,
  input  [15:0] Contents_of_Rb,
  input  [15:0] Current_Value_of_PC,
  input  [4:0] Current_Flags,
  output [15:0] New_Value_of_PC
);

  wire bitselector_1_out, bitselector_2_out, bitselector_3_out, bitselector_5_out, not_1_out, or_1_out,
       xor_1_out;
  wire [7:0] bitselector_4_out;
  wire [15:0] adder_1_out, adder_2_out, bit_extender_1_out, multiplexer_1_out;

  BitSelector #(.width(5)) bitselector_1 (.in(Current_Flags), .out(bitselector_1_out), .sel(3'b000));
  BitSelector #(.width(5)) bitselector_2 (.in(Current_Flags), .out(bitselector_2_out), .sel(3'b010));
  BitSelector #(.width(5)) bitselector_3 (.in(Current_Flags), .out(bitselector_3_out), .sel(3'b001));
  BitSelector #(.width(16), .group(8)) bitselector_4 (.in(Op_Code), .out(bitselector_4_out), .sel(1'b0));
  BitSelector #(.width(16)) bitselector_5 (.in(Op_Code), .out(bitselector_5_out), .sel(4'b1100));
  assign bit_extender_1_out = {{8{bitselector_4_out[7]}}, bitselector_4_out};  // Bit_Extender bit_extender_1
  Adder #(.width(16)) adder_1 (.a(bit_extender_1_out), .b(Current_Value_of_PC), .out(adder_1_out));  // open: cin, cout
  not not_1 (not_1_out, bitselector_5_out);
  xor xor_1 (xor_1_out, bitselector_1_out, bitselector_2_out);
  or or_1 (or_1_out, xor_1_out, bitselector_3_out);
  Multiplexer #(.width(16)) multiplexer_1 (
    .in0(Contents_of_Rb), .in1(adder_1_out), .out(multiplexer_1_out), .sel(not_1_out));  // open: en
  Adder #(.width(16)) adder_2 (.a(Current_Value_of_PC), .b(16'h1), .out(adder_2_out));  // open: cin, cout
  Multiplexer #(.width(16)) multiplexer_2 (
    .in0(adder_2_out), .in1(multiplexer_1_out), .out(New_Value_of_PC), .sel(or_1_out));  // open: en

  // Notes on the sheet:
  //   o (bits 0-7)
  //   v
  //   z
  //   bit 12
  //   s
  //   BLE
  //   BLER
endmodule

module BG_BGR (
  input  [15:0] Op_Code,
  input  [15:0] Contents_of_Rb,
  input  [15:0] Current_Value_of_PC,
  input  [4:0] Current_Flags,
  output [15:0] New_Value_of_PC
);

  wire bitselector_1_out, bitselector_2_out, bitselector_3_out, bitselector_5_out, not_1_out, not_2_out,
       or_1_out, xor_1_out;
  wire [7:0] bitselector_4_out;
  wire [15:0] adder_1_out, adder_2_out, bit_extender_1_out, multiplexer_1_out;

  BitSelector #(.width(5)) bitselector_1 (.in(Current_Flags), .out(bitselector_1_out), .sel(3'b000));
  BitSelector #(.width(5)) bitselector_2 (.in(Current_Flags), .out(bitselector_2_out), .sel(3'b010));
  BitSelector #(.width(5)) bitselector_3 (.in(Current_Flags), .out(bitselector_3_out), .sel(3'b001));
  BitSelector #(.width(16), .group(8)) bitselector_4 (.in(Op_Code), .out(bitselector_4_out), .sel(1'b0));
  BitSelector #(.width(16)) bitselector_5 (.in(Op_Code), .out(bitselector_5_out), .sel(4'b1100));
  assign bit_extender_1_out = {{8{bitselector_4_out[7]}}, bitselector_4_out};  // Bit_Extender bit_extender_1
  Adder #(.width(16)) adder_1 (.a(bit_extender_1_out), .b(Current_Value_of_PC), .out(adder_1_out));  // open: cin, cout
  not not_1 (not_1_out, bitselector_5_out);
  xor xor_1 (xor_1_out, bitselector_1_out, bitselector_2_out);
  or or_1 (or_1_out, xor_1_out, bitselector_3_out);
  Multiplexer #(.width(16)) multiplexer_1 (
    .in0(Contents_of_Rb), .in1(adder_1_out), .out(multiplexer_1_out), .sel(not_1_out));  // open: en
  not not_2 (not_2_out, or_1_out);
  Adder #(.width(16)) adder_2 (.a(Current_Value_of_PC), .b(16'h1), .out(adder_2_out));  // open: cin, cout
  Multiplexer #(.width(16)) multiplexer_2 (
    .in0(adder_2_out), .in1(multiplexer_1_out), .out(New_Value_of_PC), .sel(not_2_out));  // open: en

  // Notes on the sheet:
  //   o (bits 0-7)
  //   v
  //   z
  //   bit 12
  //   s
  //   BG
  //   BGR
endmodule

module BULE_BULER (
  input  [15:0] Op_Code,
  input  [15:0] Contents_of_Rb,
  input  [15:0] Current_Value_of_PC,
  input  [4:0] Current_Flags,
  output [15:0] New_Value_of_PC
);

  wire bitselector_1_out, bitselector_2_out, bitselector_4_out, not_1_out, not_2_out, or_1_out;
  wire [7:0] bitselector_3_out;
  wire [15:0] adder_1_out, adder_2_out, bit_extender_1_out, multiplexer_1_out;

  BitSelector #(.width(5)) bitselector_1 (.in(Current_Flags), .out(bitselector_1_out), .sel(3'b011));
  BitSelector #(.width(5)) bitselector_2 (.in(Current_Flags), .out(bitselector_2_out), .sel(3'b001));
  BitSelector #(.width(16), .group(8)) bitselector_3 (.in(Op_Code), .out(bitselector_3_out), .sel(1'b0));
  BitSelector #(.width(16)) bitselector_4 (.in(Op_Code), .out(bitselector_4_out), .sel(4'b1100));
  not not_1 (not_1_out, bitselector_1_out);
  assign bit_extender_1_out = {{8{bitselector_3_out[7]}}, bitselector_3_out};  // Bit_Extender bit_extender_1
  Adder #(.width(16)) adder_1 (.a(bit_extender_1_out), .b(Current_Value_of_PC), .out(adder_1_out));  // open: cin, cout
  not not_2 (not_2_out, bitselector_4_out);
  or or_1 (or_1_out, not_1_out, bitselector_2_out);
  Multiplexer #(.width(16)) multiplexer_1 (
    .in0(Contents_of_Rb), .in1(adder_1_out), .out(multiplexer_1_out), .sel(not_2_out));  // open: en
  Adder #(.width(16)) adder_2 (.a(Current_Value_of_PC), .b(16'h1), .out(adder_2_out));  // open: cin, cout
  Multiplexer #(.width(16)) multiplexer_2 (
    .in0(adder_2_out), .in1(multiplexer_1_out), .out(New_Value_of_PC), .sel(or_1_out));  // open: en

  // Notes on the sheet:
  //   o (bits 0-7)
  //   z
  //   bit 12
  //   c
  //   BULE
  //   BULER
endmodule

module BUG_BUGR (
  input  [15:0] Op_Code,
  input  [15:0] Contents_of_Rb,
  input  [15:0] Current_Value_of_PC,
  input  [4:0] Current_Flags,
  output [15:0] New_Value_of_PC
);

  wire bitselector_1_out, bitselector_2_out, bitselector_4_out, not_1_out, not_2_out, not_3_out, or_1_out;
  wire [7:0] bitselector_3_out;
  wire [15:0] adder_1_out, adder_2_out, bit_extender_1_out, multiplexer_1_out;

  BitSelector #(.width(5)) bitselector_1 (.in(Current_Flags), .out(bitselector_1_out), .sel(3'b011));
  BitSelector #(.width(5)) bitselector_2 (.in(Current_Flags), .out(bitselector_2_out), .sel(3'b001));
  BitSelector #(.width(16), .group(8)) bitselector_3 (.in(Op_Code), .out(bitselector_3_out), .sel(1'b0));
  BitSelector #(.width(16)) bitselector_4 (.in(Op_Code), .out(bitselector_4_out), .sel(4'b1100));
  not not_1 (not_1_out, bitselector_1_out);
  assign bit_extender_1_out = {{8{bitselector_3_out[7]}}, bitselector_3_out};  // Bit_Extender bit_extender_1
  Adder #(.width(16)) adder_1 (.a(bit_extender_1_out), .b(Current_Value_of_PC), .out(adder_1_out));  // open: cin, cout
  not not_2 (not_2_out, bitselector_4_out);
  or or_1 (or_1_out, not_1_out, bitselector_2_out);
  Multiplexer #(.width(16)) multiplexer_1 (
    .in0(Contents_of_Rb), .in1(adder_1_out), .out(multiplexer_1_out), .sel(not_2_out));  // open: en
  not not_3 (not_3_out, or_1_out);
  Adder #(.width(16)) adder_2 (.a(Current_Value_of_PC), .b(16'h1), .out(adder_2_out));  // open: cin, cout
  Multiplexer #(.width(16)) multiplexer_2 (
    .in0(adder_2_out), .in1(multiplexer_1_out), .out(New_Value_of_PC), .sel(not_3_out));  // open: en

  // Notes on the sheet:
  //   o (bits 0-7)
  //   z
  //   bit 12
  //   c
  //   BUG
  //   BUGR
endmodule

module BZ_BZR (
  input  [15:0] Op_Code,
  input  [15:0] Contents_of_Rb,
  input  [15:0] Current_Value_of_PC,
  input  [4:0] Current_Flags,
  output [15:0] New_Value_of_PC
);

  wire bitselector_1_out, bitselector_3_out, not_1_out;
  wire [7:0] bitselector_2_out;
  wire [15:0] adder_1_out, adder_2_out, bit_extender_1_out, multiplexer_1_out;

  BitSelector #(.width(5)) bitselector_1 (.in(Current_Flags), .out(bitselector_1_out), .sel(3'b001));
  BitSelector #(.width(16), .group(8)) bitselector_2 (.in(Op_Code), .out(bitselector_2_out), .sel(1'b0));
  BitSelector #(.width(16)) bitselector_3 (.in(Op_Code), .out(bitselector_3_out), .sel(4'b1100));
  assign bit_extender_1_out = {{8{bitselector_2_out[7]}}, bitselector_2_out};  // Bit_Extender bit_extender_1
  Adder #(.width(16)) adder_1 (.a(bit_extender_1_out), .b(Current_Value_of_PC), .out(adder_1_out));  // open: cin, cout
  not not_1 (not_1_out, bitselector_3_out);
  Multiplexer #(.width(16)) multiplexer_1 (
    .in0(Contents_of_Rb), .in1(adder_1_out), .out(multiplexer_1_out), .sel(not_1_out));  // open: en
  Adder #(.width(16)) adder_2 (.a(Current_Value_of_PC), .b(16'h1), .out(adder_2_out));  // open: cin, cout
  Multiplexer #(.width(16)) multiplexer_2 (
    .in0(adder_2_out), .in1(multiplexer_1_out), .out(New_Value_of_PC), .sel(bitselector_1_out));  // open: en

  // Notes on the sheet:
  //   o (bits 0-7)
  //   z
  //   bit 12
  //   BZ
  //   BZR
endmodule

module BNZ_BNZR (
  input  [15:0] Op_Code,
  input  [15:0] Contents_of_Rb,
  input  [15:0] Current_Value_of_PC,
  input  [4:0] Current_Flags,
  output [15:0] New_Value_of_PC
);

  wire bitselector_1_out, bitselector_3_out, not_1_out, not_2_out;
  wire [7:0] bitselector_2_out;
  wire [15:0] adder_1_out, adder_2_out, bit_extender_1_out, multiplexer_1_out;

  BitSelector #(.width(5)) bitselector_1 (.in(Current_Flags), .out(bitselector_1_out), .sel(3'b001));
  BitSelector #(.width(16), .group(8)) bitselector_2 (.in(Op_Code), .out(bitselector_2_out), .sel(1'b0));
  BitSelector #(.width(16)) bitselector_3 (.in(Op_Code), .out(bitselector_3_out), .sel(4'b1100));
  not not_1 (not_1_out, bitselector_1_out);
  assign bit_extender_1_out = {{8{bitselector_2_out[7]}}, bitselector_2_out};  // Bit_Extender bit_extender_1
  Adder #(.width(16)) adder_1 (.a(bit_extender_1_out), .b(Current_Value_of_PC), .out(adder_1_out));  // open: cin, cout
  not not_2 (not_2_out, bitselector_3_out);
  Multiplexer #(.width(16)) multiplexer_1 (
    .in0(Contents_of_Rb), .in1(adder_1_out), .out(multiplexer_1_out), .sel(not_2_out));  // open: en
  Adder #(.width(16)) adder_2 (.a(Current_Value_of_PC), .b(16'h1), .out(adder_2_out));  // open: cin, cout
  Multiplexer #(.width(16)) multiplexer_2 (
    .in0(adder_2_out), .in1(multiplexer_1_out), .out(New_Value_of_PC), .sel(not_1_out));  // open: en

  // Notes on the sheet:
  //   o (bits 0-7)
  //   z
  //   bit 12
  //   BNZ
  //   BNZR
endmodule

module BC_BCR (
  input  [15:0] Op_Code,
  input  [15:0] Contents_of_Rb,
  input  [15:0] Current_Value_of_PC,
  input  [4:0] Current_Flags,
  output [15:0] New_Value_of_PC
);

  wire bitselector_1_out, bitselector_3_out, not_1_out;
  wire [7:0] bitselector_2_out;
  wire [15:0] adder_1_out, adder_2_out, bit_extender_1_out, multiplexer_1_out;

  BitSelector #(.width(5)) bitselector_1 (.in(Current_Flags), .out(bitselector_1_out), .sel(3'b011));
  BitSelector #(.width(16), .group(8)) bitselector_2 (.in(Op_Code), .out(bitselector_2_out), .sel(1'b0));
  BitSelector #(.width(16)) bitselector_3 (.in(Op_Code), .out(bitselector_3_out), .sel(4'b1100));
  assign bit_extender_1_out = {{8{bitselector_2_out[7]}}, bitselector_2_out};  // Bit_Extender bit_extender_1
  Adder #(.width(16)) adder_1 (.a(bit_extender_1_out), .b(Current_Value_of_PC), .out(adder_1_out));  // open: cin, cout
  not not_1 (not_1_out, bitselector_3_out);
  Multiplexer #(.width(16)) multiplexer_1 (
    .in0(Contents_of_Rb), .in1(adder_1_out), .out(multiplexer_1_out), .sel(not_1_out));  // open: en
  Adder #(.width(16)) adder_2 (.a(Current_Value_of_PC), .b(16'h1), .out(adder_2_out));  // open: cin, cout
  Multiplexer #(.width(16)) multiplexer_2 (
    .in0(adder_2_out), .in1(multiplexer_1_out), .out(New_Value_of_PC), .sel(bitselector_1_out));  // open: en

  // Notes on the sheet:
  //   o (bits 0-7)
  //   c
  //   bit 12
  //   BC
  //   BCR
endmodule

module BNC_BNCR (
  input  [15:0] Op_Code,
  input  [15:0] Contents_of_Rb,
  input  [15:0] Current_Value_of_PC,
  input  [4:0] Current_Flags,
  output [15:0] New_Value_of_PC
);

  wire bitselector_1_out, bitselector_3_out, not_1_out, not_2_out;
  wire [7:0] bitselector_2_out;
  wire [15:0] adder_1_out, adder_2_out, bit_extender_1_out, multiplexer_1_out;

  BitSelector #(.width(5)) bitselector_1 (.in(Current_Flags), .out(bitselector_1_out), .sel(3'b011));
  BitSelector #(.width(16), .group(8)) bitselector_2 (.in(Op_Code), .out(bitselector_2_out), .sel(1'b0));
  BitSelector #(.width(16)) bitselector_3 (.in(Op_Code), .out(bitselector_3_out), .sel(4'b1100));
  assign bit_extender_1_out = {{8{bitselector_2_out[7]}}, bitselector_2_out};  // Bit_Extender bit_extender_1
  Adder #(.width(16)) adder_1 (.a(bit_extender_1_out), .b(Current_Value_of_PC), .out(adder_1_out));  // open: cin, cout
  not not_1 (not_1_out, bitselector_3_out);
  not not_2 (not_2_out, bitselector_1_out);
  Multiplexer #(.width(16)) multiplexer_1 (
    .in0(Contents_of_Rb), .in1(adder_1_out), .out(multiplexer_1_out), .sel(not_1_out));  // open: en
  Adder #(.width(16)) adder_2 (.a(Current_Value_of_PC), .b(16'h1), .out(adder_2_out));  // open: cin, cout
  Multiplexer #(.width(16)) multiplexer_2 (
    .in0(adder_2_out), .in1(multiplexer_1_out), .out(New_Value_of_PC), .sel(not_2_out));  // open: en

  // Notes on the sheet:
  //   o (bits 0-7)
  //   c
  //   bit 12
  //   BNC
  //   BNCR
endmodule

module BS_BSR (
  input  [15:0] Op_Code,
  input  [15:0] Contents_of_Rb,
  input  [15:0] Current_Value_of_PC,
  input  [4:0] Current_Flags,
  output [15:0] New_Value_of_PC
);

  wire bitselector_1_out, bitselector_3_out, not_1_out;
  wire [7:0] bitselector_2_out;
  wire [15:0] adder_1_out, adder_2_out, bit_extender_1_out, multiplexer_1_out;

  BitSelector #(.width(5)) bitselector_1 (.in(Current_Flags), .out(bitselector_1_out), .sel(3'b000));
  BitSelector #(.width(16), .group(8)) bitselector_2 (.in(Op_Code), .out(bitselector_2_out), .sel(1'b0));
  BitSelector #(.width(16)) bitselector_3 (.in(Op_Code), .out(bitselector_3_out), .sel(4'b1100));
  assign bit_extender_1_out = {{8{bitselector_2_out[7]}}, bitselector_2_out};  // Bit_Extender bit_extender_1
  Adder #(.width(16)) adder_1 (.a(bit_extender_1_out), .b(Current_Value_of_PC), .out(adder_1_out));  // open: cin, cout
  not not_1 (not_1_out, bitselector_3_out);
  Multiplexer #(.width(16)) multiplexer_1 (
    .in0(Contents_of_Rb), .in1(adder_1_out), .out(multiplexer_1_out), .sel(not_1_out));  // open: en
  Adder #(.width(16)) adder_2 (.a(Current_Value_of_PC), .b(16'h1), .out(adder_2_out));  // open: cin, cout
  Multiplexer #(.width(16)) multiplexer_2 (
    .in0(adder_2_out), .in1(multiplexer_1_out), .out(New_Value_of_PC), .sel(bitselector_1_out));  // open: en

  // Notes on the sheet:
  //   o (bits 0-7)
  //   s
  //   bit 12
  //   BS
  //   BSR
endmodule

module BNS_BNSR (
  input  [15:0] Op_Code,
  input  [15:0] Contents_of_Rb,
  input  [15:0] Current_Value_of_PC,
  input  [4:0] Current_Flags,
  output [15:0] New_Value_of_PC
);

  wire bitselector_1_out, bitselector_3_out, not_1_out, not_2_out;
  wire [7:0] bitselector_2_out;
  wire [15:0] adder_1_out, adder_2_out, bit_extender_1_out, multiplexer_1_out;

  BitSelector #(.width(5)) bitselector_1 (.in(Current_Flags), .out(bitselector_1_out), .sel(3'b000));
  BitSelector #(.width(16), .group(8)) bitselector_2 (.in(Op_Code), .out(bitselector_2_out), .sel(1'b0));
  BitSelector #(.width(16)) bitselector_3 (.in(Op_Code), .out(bitselector_3_out), .sel(4'b1100));
  assign bit_extender_1_out = {{8{bitselector_2_out[7]}}, bitselector_2_out};  // Bit_Extender bit_extender_1
  Adder #(.width(16)) adder_1 (.a(bit_extender_1_out), .b(Current_Value_of_PC), .out(adder_1_out));  // open: cin, cout
  not not_1 (not_1_out, bitselector_3_out);
  not not_2 (not_2_out, bitselector_1_out);
  Multiplexer #(.width(16)) multiplexer_1 (
    .in0(Contents_of_Rb), .in1(adder_1_out), .out(multiplexer_1_out), .sel(not_1_out));  // open: en
  Adder #(.width(16)) adder_2 (.a(Current_Value_of_PC), .b(16'h1), .out(adder_2_out));  // open: cin, cout
  Multiplexer #(.width(16)) multiplexer_2 (
    .in0(adder_2_out), .in1(multiplexer_1_out), .out(New_Value_of_PC), .sel(not_2_out));  // open: en

  // Notes on the sheet:
  //   o (bits 0-7)
  //   s
  //   bit 12
  //   BNS
  //   BNSR
endmodule

module BV_BVR (
  input  [15:0] Op_Code,
  input  [15:0] Contents_of_Rb,
  input  [15:0] Current_Value_of_PC,
  input  [4:0] Current_Flags,
  output [15:0] New_Value_of_PC
);

  wire bitselector_1_out, bitselector_3_out, not_1_out;
  wire [7:0] bitselector_2_out;
  wire [15:0] adder_1_out, adder_2_out, bit_extender_1_out, multiplexer_1_out;

  BitSelector #(.width(5)) bitselector_1 (.in(Current_Flags), .out(bitselector_1_out), .sel(3'b010));
  BitSelector #(.width(16), .group(8)) bitselector_2 (.in(Op_Code), .out(bitselector_2_out), .sel(1'b0));
  BitSelector #(.width(16)) bitselector_3 (.in(Op_Code), .out(bitselector_3_out), .sel(4'b1100));
  assign bit_extender_1_out = {{8{bitselector_2_out[7]}}, bitselector_2_out};  // Bit_Extender bit_extender_1
  Adder #(.width(16)) adder_1 (.a(bit_extender_1_out), .b(Current_Value_of_PC), .out(adder_1_out));  // open: cin, cout
  not not_1 (not_1_out, bitselector_3_out);
  Multiplexer #(.width(16)) multiplexer_1 (
    .in0(Contents_of_Rb), .in1(adder_1_out), .out(multiplexer_1_out), .sel(not_1_out));  // open: en
  Adder #(.width(16)) adder_2 (.a(Current_Value_of_PC), .b(16'h1), .out(adder_2_out));  // open: cin, cout
  Multiplexer #(.width(16)) multiplexer_2 (
    .in0(adder_2_out), .in1(multiplexer_1_out), .out(New_Value_of_PC), .sel(bitselector_1_out));  // open: en

  // Notes on the sheet:
  //   o (bits 0-7)
  //   v
  //   bit 12
  //   BV
  //   BVR
endmodule

module BNV_BNVR (
  input  [15:0] Op_Code,
  input  [15:0] Contents_of_Rb,
  input  [15:0] Current_Value_of_PC,
  input  [4:0] Current_Flags,
  output [15:0] New_Value_of_PC
);

  wire bitselector_1_out, bitselector_3_out, not_1_out, not_2_out;
  wire [7:0] bitselector_2_out;
  wire [15:0] adder_1_out, adder_2_out, bit_extender_1_out, multiplexer_1_out;

  BitSelector #(.width(5)) bitselector_1 (.in(Current_Flags), .out(bitselector_1_out), .sel(3'b010));
  BitSelector #(.width(16), .group(8)) bitselector_2 (.in(Op_Code), .out(bitselector_2_out), .sel(1'b0));
  BitSelector #(.width(16)) bitselector_3 (.in(Op_Code), .out(bitselector_3_out), .sel(4'b1100));
  not not_1 (not_1_out, bitselector_1_out);
  assign bit_extender_1_out = {{8{bitselector_2_out[7]}}, bitselector_2_out};  // Bit_Extender bit_extender_1
  Adder #(.width(16)) adder_1 (.a(bit_extender_1_out), .b(Current_Value_of_PC), .out(adder_1_out));  // open: cin, cout
  not not_2 (not_2_out, bitselector_3_out);
  Multiplexer #(.width(16)) multiplexer_1 (
    .in0(Contents_of_Rb), .in1(adder_1_out), .out(multiplexer_1_out), .sel(not_2_out));  // open: en
  Adder #(.width(16)) adder_2 (.a(Current_Value_of_PC), .b(16'h1), .out(adder_2_out));  // open: cin, cout
  Multiplexer #(.width(16)) multiplexer_2 (
    .in0(adder_2_out), .in1(multiplexer_1_out), .out(New_Value_of_PC), .sel(not_1_out));  // open: en

  // Notes on the sheet:
  //   o (bits 0-7)
  //   v
  //   bit 12
  //   BNV
  //   BNVR
endmodule

module Load_Flags (
  input  [4:0] Current_Flags,
  input  [15:0] M_Rb___o,
  output [4:0] Updated_Flags
);

  BitSelector #(.width(16)) bitselector_1 (.in(M_Rb___o), .out(Updated_Flags[0]), .sel(4'b1111));
  Comparator #(.width(16)) comparator_1 (.a(M_Rb___o), .b({16{1'b0}}), .eq(Updated_Flags[1]));  // open: gt, lt

  assign Updated_Flags[4:2] = Current_Flags[4:2];

  // Notes on the sheet:
  //   z
  //   s
endmodule

module Rb___o (
  input  [15:0] Op_Code,
  input  [15:0] Contents_of_Rb,
  output [15:0] Rb___o
);

  wire bitselector_1_out;
  wire [3:0] bitselector_2_out;
  wire [4:0] adder_1_out, bit_extender_1_out, bit_extender_2_out, shifter_1_out;
  wire [15:0] bit_extender_3_out;

  BitSelector #(.width(16)) bitselector_1 (.in(Op_Code), .out(bitselector_1_out), .sel(4'b1100));
  BitSelector #(.width(16), .group(4)) bitselector_2 (.in(Op_Code), .out(bitselector_2_out), .sel(2'b01));
  assign bit_extender_1_out = {{4{1'b0}}, bitselector_1_out};  // Bit_Extender bit_extender_1
  Shifter #(.width(5)) shifter_1 (.in(bit_extender_1_out), .\dist (3'b100), .out(shifter_1_out));
  assign bit_extender_2_out = {{1{1'b0}}, bitselector_2_out};  // Bit_Extender bit_extender_2
  Adder #(.width(5)) adder_1 (.a(shifter_1_out), .b(bit_extender_2_out), .out(adder_1_out));  // open: cin, cout
  assign bit_extender_3_out = {{11{1'b0}}, adder_1_out};  // Bit_Extender bit_extender_3
  Adder #(.width(16)) adder_2 (.a(bit_extender_3_out), .b(Contents_of_Rb), .out(Rb___o));  // open: cin, cout

  // Notes on the sheet:
  //   o4
  //   o3 o2 o1 o0
  //   o4 o3 o2 o1 o1 o0
  //   Rb + o
endmodule
