// Logisim project Shadow Register.circ as structural Verilog: 1 circuit, main circuit main
module main (
  input  Start_Interrupt,
  input  Return_from_interrupt,
  input  Enable_Reg,
  input  [7:0] Set_Value
);

  wire and_1_out, clock_1_out, not_1_out, or_1_out, s_r_ff_1_q;
  wire [7:0] multiplexer_1_out, multiplexer_2_out, register_1_q, register_2_q;

  Clock clock_1 (.out(clock_1_out));
  or or_1 (or_1_out, Return_from_interrupt, Enable_Reg);
  S_R_Flip_Flop s_r_ff_1 (
    .S(Start_Interrupt), .clk(clock_1_out), .R(Return_from_interrupt), .Q(s_r_ff_1_q), .en(1'b1));  // open: Qn, preset, reset
  Multiplexer #(.width(8)) multiplexer_1 (
    .in0(Set_Value), .in1(register_2_q), .out(multiplexer_1_out), .sel(Return_from_interrupt));  // open: en
  and and_1 (and_1_out, or_1_out, not_1_out);
  Register register_1 (.D(multiplexer_1_out), .en(or_1_out), .Q(register_1_q), .clk(clock_1_out));  // open: clr
  not not_1 (not_1_out, s_r_ff_1_q);
  Register register_2 (.D(multiplexer_1_out), .en(and_1_out), .Q(register_2_q), .clk(clock_1_out));  // open: clr
  Multiplexer #(.width(8)) multiplexer_2 (
    .in0(register_2_q), .in1(register_1_q), .out(multiplexer_2_out), .sel(s_r_ff_1_q));  // open: en
  // Probe on multiplexer_2_out
endmodule
